// Logisim project EP3-2.circ as structural Verilog: 15 circuits, main circuit ALU
module ALU (
  input  [15:0] in_1,
  input  [15:0] in_2,
  input  [2:0] Op,
  output Overflow,
  output [15:0] out_5
);

  wire adder_1_out_3, divider_1_out_5, multiplier_1_overflow, subtractor_1_overflow;
  wire [15:0] adder_1_out_4, divider_1_quociente, divider_1_resto, multiplier_1_produto, subtractor_1_produto;
  wire [31:0] demultiplexer_1_out0, demultiplexer_1_out1, demultiplexer_1_out2, demultiplexer_1_out3,
       demultiplexer_1_out4, multiplexer_1_out;

  Demultiplexer #(.select(3), .width(32), .disabled(0), .enable("false")) demultiplexer_1 (
    .out0(demultiplexer_1_out0), .out1(demultiplexer_1_out1), .out2(demultiplexer_1_out2),
    .out3(demultiplexer_1_out3), .out4(demultiplexer_1_out4), .in({in_2, in_1}), .sel(Op));  // open: out5, out6, out7
  Multiplexer #(.width(32), .enable("false")) multiplexer_1 (
    .in0(demultiplexer_1_out3), .in1(demultiplexer_1_out4), .out(multiplexer_1_out), .sel(Op[2]));
  adder adder_1 (
    .in_1(demultiplexer_1_out0[15:0]), .in_2(demultiplexer_1_out0[31:16]), .out_4(adder_1_out_4),
    .out_3(adder_1_out_3));
  subtractor subtractor_1 (
    .A(demultiplexer_1_out1[15:0]), .B(demultiplexer_1_out1[31:16]), .produto(subtractor_1_produto),
    .overflow(subtractor_1_overflow));
  multiplier multiplier_1 (
    .A(demultiplexer_1_out2[15:0]), .produto(multiplier_1_produto), .B(demultiplexer_1_out2[31:16]),
    .overflow(multiplier_1_overflow));
  divider divider_1 (
    .A(multiplexer_1_out[15:0]), .B(multiplexer_1_out[31:16]), .Quociente(divider_1_quociente),
    .Resto(divider_1_resto), .out_5(divider_1_out_5));
  Pull_Resistor pull_resistor_1 (.node(Overflow));
  Multiplexer #(.select(3), .disabled(0), .enable("false")) multiplexer_2 (
    .in0(adder_1_out_3), .in1(subtractor_1_overflow), .in2(multiplier_1_overflow), .in3(divider_1_out_5),
    .in4(divider_1_out_5), .out(Overflow), .sel(Op));  // open: in5, in6, in7
  Multiplexer #(.select(3), .width(16), .disabled(0), .enable("false")) multiplexer_3 (
    .in0(adder_1_out_4), .in1(subtractor_1_produto), .in2(multiplier_1_produto), .in3(divider_1_quociente),
    .in4(divider_1_resto), .out(out_5), .sel(Op));  // open: in5, in6, in7

  // Other names for the same wires on the sheet: choice[2:0] = Op

  // Notes on the sheet:
  //   A
  //   B
  //   Resultado
endmodule

module PC (
  input  clear,
  input  clock,
  input  set,
  input  [7:0] in_4,
  output [7:0] out_5
);

  wire and_1_out, and_2_out, and_3_out, and_4_out, and_5_out, and_6_out, and_7_out, controlled_buffer_1_out,
       controlled_buffer_4_out, controlled_buffer_6_out, controlled_buffer_7_out, controlled_buffer_9_out,
       controlled_buffer_11_out, controlled_buffer_13_out, controlled_buffer_15_out,
       controlled_buffer_17_out, not_1_out, not_2_out, not_3_out, not_4_out, not_5_out, not_6_out, not_7_out,
       not_8_out, not_9_out, not_10_out, not_11_out, not_12_out, not_13_out, not_14_out, not_15_out,
       not_16_out, not_17_out, not_18_out, not_19_out, not_20_out, not_21_out, not_22_out, not_23_out,
       not_24_out, not_25_out, not_26_out, not_27_out, pull_resistor_1_node, pull_resistor_2_node,
       pull_resistor_3_node, pull_resistor_4_node, pull_resistor_5_node, pull_resistor_6_node,
       pull_resistor_7_node, pull_resistor_8_node;

  and and_1 (and_1_out, out_5[0], out_5[1], out_5[2], out_5[3], out_5[4], out_5[5], out_5[6]);
  assign controlled_buffer_1_out = not_3_out ? controlled_buffer_17_out : 1'bz;  // Controlled_Buffer controlled_buffer_1
  not not_1 (not_1_out, not_2_out);
  not not_2 (not_2_out, pull_resistor_1_node);
  not not_3 (not_3_out, and_7_out);
  Pull_Resistor pull_resistor_1 (.node(pull_resistor_1_node));
  assign pull_resistor_1_node = and_7_out ? in_4[7] : 1'bz;  // Controlled_Buffer controlled_buffer_2
  and and_2 (and_2_out, out_5[0], out_5[1], out_5[2], out_5[3], out_5[4], out_5[5]);
  J_K_Flip_Flop j_k_ff_1 (
    .J(and_1_out), .clk(not_26_out), .K(and_1_out), .Q(out_5[7]), .preset(not_1_out), .en(1'b1),
    .reset(controlled_buffer_1_out));  // open: Qn
  not not_4 (not_4_out, not_5_out);
  not not_5 (not_5_out, pull_resistor_2_node);
  assign controlled_buffer_1_out = and_7_out ? ~in_4[7] : 1'bz;  // Controlled_Inverter controlled_inverter_1
  Pull_Resistor pull_resistor_2 (.node(pull_resistor_2_node));
  assign pull_resistor_2_node = and_7_out ? in_4[6] : 1'bz;  // Controlled_Buffer controlled_buffer_3
  and and_3 (and_3_out, out_5[0], out_5[1], out_5[2], out_5[3], out_5[4]);
  J_K_Flip_Flop j_k_ff_2 (
    .J(and_2_out), .clk(not_26_out), .K(and_2_out), .Q(out_5[6]), .preset(not_4_out), .en(1'b1),
    .reset(controlled_buffer_4_out));  // open: Qn
  assign controlled_buffer_4_out = not_8_out ? controlled_buffer_17_out : 1'bz;  // Controlled_Buffer controlled_buffer_4
  not not_6 (not_6_out, not_7_out);
  not not_7 (not_7_out, pull_resistor_3_node);
  not not_8 (not_8_out, and_7_out);
  assign controlled_buffer_4_out = and_7_out ? ~in_4[6] : 1'bz;  // Controlled_Inverter controlled_inverter_2
  Pull_Resistor pull_resistor_3 (.node(pull_resistor_3_node));
  assign pull_resistor_3_node = and_7_out ? in_4[5] : 1'bz;  // Controlled_Buffer controlled_buffer_5
  J_K_Flip_Flop j_k_ff_3 (
    .J(and_3_out), .clk(not_26_out), .K(and_3_out), .Q(out_5[5]), .preset(not_6_out), .en(1'b1),
    .reset(controlled_buffer_6_out));  // open: Qn
  assign controlled_buffer_6_out = not_9_out ? controlled_buffer_17_out : 1'bz;  // Controlled_Buffer controlled_buffer_6
  not not_9 (not_9_out, and_7_out);
  assign controlled_buffer_6_out = and_7_out ? ~in_4[5] : 1'bz;  // Controlled_Inverter controlled_inverter_3
  and and_4 (and_4_out, out_5[0], out_5[1], out_5[2], out_5[3]);
  J_K_Flip_Flop j_k_ff_4 (
    .J(and_4_out), .clk(not_26_out), .K(and_4_out), .Q(out_5[4]), .preset(not_10_out), .en(1'b1),
    .reset(controlled_buffer_7_out));  // open: Qn
  assign controlled_buffer_7_out = not_12_out ? controlled_buffer_17_out : 1'bz;  // Controlled_Buffer controlled_buffer_7
  not not_10 (not_10_out, not_11_out);
  not not_11 (not_11_out, pull_resistor_4_node);
  not not_12 (not_12_out, and_7_out);
  Pull_Resistor pull_resistor_4 (.node(pull_resistor_4_node));
  assign controlled_buffer_7_out = and_7_out ? ~in_4[4] : 1'bz;  // Controlled_Inverter controlled_inverter_4
  assign pull_resistor_4_node = and_7_out ? in_4[4] : 1'bz;  // Controlled_Buffer controlled_buffer_8
  and and_5 (and_5_out, out_5[0], out_5[1], out_5[2]);
  J_K_Flip_Flop j_k_ff_5 (
    .J(and_5_out), .clk(not_26_out), .K(and_5_out), .Q(out_5[3]), .preset(not_13_out), .en(1'b1),
    .reset(controlled_buffer_9_out));  // open: Qn
  assign controlled_buffer_9_out = not_15_out ? controlled_buffer_17_out : 1'bz;  // Controlled_Buffer controlled_buffer_9
  not not_13 (not_13_out, not_14_out);
  not not_14 (not_14_out, pull_resistor_5_node);
  not not_15 (not_15_out, and_7_out);
  Pull_Resistor pull_resistor_5 (.node(pull_resistor_5_node));
  assign controlled_buffer_9_out = and_7_out ? ~in_4[3] : 1'bz;  // Controlled_Inverter controlled_inverter_5
  assign pull_resistor_5_node = and_7_out ? in_4[3] : 1'bz;  // Controlled_Buffer controlled_buffer_10
  J_K_Flip_Flop j_k_ff_6 (
    .J(and_6_out), .clk(not_26_out), .K(and_6_out), .Q(out_5[2]), .preset(not_16_out), .en(1'b1),
    .reset(controlled_buffer_11_out));  // open: Qn
  assign controlled_buffer_11_out = not_18_out ? controlled_buffer_17_out : 1'bz;  // Controlled_Buffer controlled_buffer_11
  not not_16 (not_16_out, not_17_out);
  not not_17 (not_17_out, pull_resistor_6_node);
  not not_18 (not_18_out, and_7_out);
  assign controlled_buffer_11_out = and_7_out ? ~in_4[2] : 1'bz;  // Controlled_Inverter controlled_inverter_6
  Pull_Resistor pull_resistor_6 (.node(pull_resistor_6_node));
  assign pull_resistor_6_node = and_7_out ? in_4[2] : 1'bz;  // Controlled_Buffer controlled_buffer_12
  and and_6 (and_6_out, out_5[0], out_5[1]);
  J_K_Flip_Flop j_k_ff_7 (
    .J(out_5[0]), .clk(not_26_out), .K(out_5[0]), .Q(out_5[1]), .preset(not_19_out), .en(1'b1),
    .reset(controlled_buffer_13_out));  // open: Qn
  assign controlled_buffer_13_out = not_21_out ? controlled_buffer_17_out : 1'bz;  // Controlled_Buffer controlled_buffer_13
  not not_19 (not_19_out, not_20_out);
  not not_20 (not_20_out, pull_resistor_7_node);
  not not_21 (not_21_out, and_7_out);
  Pull_Resistor pull_resistor_7 (.node(pull_resistor_7_node));
  assign controlled_buffer_13_out = and_7_out ? ~in_4[1] : 1'bz;  // Controlled_Inverter controlled_inverter_7
  assign pull_resistor_7_node = and_7_out ? in_4[1] : 1'bz;  // Controlled_Buffer controlled_buffer_14
  assign controlled_buffer_15_out = not_24_out ? controlled_buffer_17_out : 1'bz;  // Controlled_Buffer controlled_buffer_15
  not not_22 (not_22_out, not_23_out);
  not not_23 (not_23_out, pull_resistor_8_node);
  not not_24 (not_24_out, and_7_out);
  Pull_Resistor pull_resistor_8 (.node(pull_resistor_8_node));
  assign pull_resistor_8_node = and_7_out ? in_4[0] : 1'bz;  // Controlled_Buffer controlled_buffer_16
  J_K_Flip_Flop j_k_ff_8 (
    .J(1'b1), .clk(not_26_out), .K(1'b1), .Q(out_5[0]), .preset(not_22_out), .en(1'b1),
    .reset(controlled_buffer_15_out));  // open: Qn
  assign controlled_buffer_17_out = not_24_out ? clear : 1'bz;  // Controlled_Buffer controlled_buffer_17
  assign controlled_buffer_15_out = and_7_out ? ~in_4[0] : 1'bz;  // Controlled_Inverter controlled_inverter_8
  not not_25 (not_25_out, not_26_out);
  and and_7 (and_7_out, not_25_out, set);
  not not_26 (not_26_out, not_27_out);
  not not_27 (not_27_out, clock);
endmodule

module Ctrl (
  input  [15:0] in_1,
  input  [15:0] in_2,
  input  clock,
  output [7:0] out_4,
  output out_5,
  output out_6,
  output out_7,
  output out_8,
  output out_9,
  output out_10,
  output out_11,
  output out_12,
  output out_13,
  output out_14,
  output out_15,
  output out_16,
  output out_17,
  output [2:0] out_18
);

  wire ADD_out, and_1_out, and_2_out, and_3_out, and_4_out, and_5_out, and_6_out, controlled_buffer_32_out,
       DIV_out, G_L, G_L0, G_L1, G_L2, G_L3, INN_out, JDZ, JDZ_out, JEQ, JEQ_out, JGE, JLE, JLT, JMP_out,
       LDA_out, MUL_out, nor_1_out, not_1_out, not_2_out, not_6_out, not_7_out, not_8_out, PRN_out, REM_out,
       STA_out, STP_out, SUB_out;
  wire [7:0] A, B;
  wire [15:0] controlled_buffer_1_out;

  and LDA (LDA_out, in_1[8], in_1[9], ~in_1[10], in_1[11], ~in_1[12], ~in_1[13], ~in_1[14], ~in_1[15]);  // AND_Gate
  and STA (STA_out, ~in_1[8], ~in_1[9], in_1[10], in_1[11], ~in_1[12], ~in_1[13], ~in_1[14], ~in_1[15]);  // AND_Gate
  and JMP (JMP_out, in_1[8], in_1[9], ~in_1[10], ~in_1[11], in_1[12], in_1[13], ~in_1[14], ~in_1[15]);  // AND_Gate
  and STP (STP_out, ~in_1[8], in_1[9], in_1[10], ~in_1[11], ~in_1[12], ~in_1[13], in_1[14], ~in_1[15]);  // AND_Gate
  and ADD (ADD_out, in_1[8], ~in_1[9], in_1[10], ~in_1[11], in_1[12], ~in_1[13], ~in_1[14], ~in_1[15]);  // AND_Gate
  and SUB (SUB_out, ~in_1[8], in_1[9], in_1[10], ~in_1[11], in_1[12], ~in_1[13], ~in_1[14], ~in_1[15]);  // AND_Gate
  and MUL (MUL_out, in_1[8], in_1[9], in_1[10], ~in_1[11], in_1[12], ~in_1[13], ~in_1[14], ~in_1[15]);  // AND_Gate
  and DIV (DIV_out, ~in_1[8], ~in_1[9], ~in_1[10], in_1[11], in_1[12], ~in_1[13], ~in_1[14], ~in_1[15]);  // AND_Gate
  and REM (REM_out, in_1[8], ~in_1[9], ~in_1[10], in_1[11], in_1[12], ~in_1[13], ~in_1[14], ~in_1[15]);  // AND_Gate
  and u_JLE (G_L0, ~in_1[8], ~in_1[9], in_1[10], ~in_1[11], in_1[12], in_1[13], ~in_1[14], ~in_1[15]);  // AND_Gate
  and u_JDZ (JDZ_out, in_1[8], ~in_1[9], in_1[10], ~in_1[11], in_1[12], in_1[13], ~in_1[14], ~in_1[15]);  // AND_Gate
  and JGT (G_L1, ~in_1[8], in_1[9], in_1[10], ~in_1[11], in_1[12], in_1[13], ~in_1[14], ~in_1[15]);  // AND_Gate
  and u_JEQ (JEQ_out, in_1[8], in_1[9], in_1[10], ~in_1[11], in_1[12], in_1[13], ~in_1[14], ~in_1[15]);  // AND_Gate
  and u_JLT (G_L2, ~in_1[8], ~in_1[9], ~in_1[10], in_1[11], in_1[12], in_1[13], ~in_1[14], ~in_1[15]);  // AND_Gate
  and u_JGE (G_L3, in_1[8], ~in_1[9], ~in_1[10], in_1[11], in_1[12], in_1[13], ~in_1[14], ~in_1[15]);  // AND_Gate
  and INN (INN_out, in_1[8], in_1[9], in_1[10], in_1[11], in_1[12], ~in_1[13], ~in_1[14], ~in_1[15]);  // AND_Gate
  and PRN (PRN_out, in_1[8], ~in_1[9], ~in_1[10], in_1[11], ~in_1[12], in_1[13], ~in_1[14], ~in_1[15]);  // AND_Gate
  assign controlled_buffer_1_out = PRN_out ? 16'h7000 : 16'bz;  // Controlled_Buffer controlled_buffer_1
  and and_1 (and_1_out, G_L3, JGE);
  assign controlled_buffer_1_out = and_1_out ? 16'h1500 : 16'bz;  // Controlled_Buffer controlled_buffer_2
  assign controlled_buffer_1_out = INN_out ? 16'ha000 : 16'bz;  // Controlled_Buffer controlled_buffer_3
  and and_2 (and_2_out, G_L2, JLT);
  assign controlled_buffer_1_out = and_2_out ? 16'h1500 : 16'bz;  // Controlled_Buffer controlled_buffer_4
  and and_3 (and_3_out, G_L1, JGE);
  assign controlled_buffer_1_out = and_3_out ? 16'h1500 : 16'bz;  // Controlled_Buffer controlled_buffer_5
  and and_4 (and_4_out, JEQ_out, JEQ);
  assign controlled_buffer_1_out = and_4_out ? 16'h1500 : 16'bz;  // Controlled_Buffer controlled_buffer_6
  and and_5 (and_5_out, G_L0, JLE);
  and and_6 (and_6_out, JDZ_out, JDZ);
  assign controlled_buffer_1_out = and_6_out ? 16'h1500 : 16'bz;  // Controlled_Buffer controlled_buffer_7
  assign controlled_buffer_1_out = REM_out ? 16'h3064 : 16'bz;  // Controlled_Buffer controlled_buffer_8
  assign controlled_buffer_1_out = and_5_out ? 16'h1500 : 16'bz;  // Controlled_Buffer controlled_buffer_9
  assign controlled_buffer_1_out = MUL_out ? 16'h3062 : 16'bz;  // Controlled_Buffer controlled_buffer_10
  assign controlled_buffer_1_out = DIV_out ? 16'h3063 : 16'bz;  // Controlled_Buffer controlled_buffer_11
  not not_1 (not_1_out, clock);
  assign controlled_buffer_1_out = SUB_out ? 16'h3061 : 16'bz;  // Controlled_Buffer controlled_buffer_12
  assign out_5 = not_1_out ? controlled_buffer_1_out[15] : 1'bz;  // Controlled_Buffer controlled_buffer_13
  Pull_Resistor pull_resistor_1 (.node(out_5));
  assign controlled_buffer_1_out = STP_out ? 16'h1480 : 16'bz;  // Controlled_Buffer controlled_buffer_14
  assign controlled_buffer_1_out = ADD_out ? 16'h3060 : 16'bz;  // Controlled_Buffer controlled_buffer_15
  assign out_6 = not_1_out ? controlled_buffer_1_out[14] : 1'bz;  // Controlled_Buffer controlled_buffer_16
  Pull_Resistor pull_resistor_2 (.node(out_6));
  assign controlled_buffer_1_out = JMP_out ? 16'h1500 : 16'bz;  // Controlled_Buffer controlled_buffer_17
  assign out_8 = not_1_out ? controlled_buffer_1_out[12] : 1'bz;  // Controlled_Buffer controlled_buffer_18
  assign out_7 = not_1_out ? controlled_buffer_1_out[13] : 1'bz;  // Controlled_Buffer controlled_buffer_19
  Pull_Resistor #(.pull(1)) pull_resistor_3 (.node(out_8));
  Pull_Resistor pull_resistor_4 (.node(out_7));
  assign controlled_buffer_1_out = LDA_out ? 16'h3810 : 16'bz;  // Controlled_Buffer controlled_buffer_20
  assign controlled_buffer_1_out = STA_out ? 16'h2200 : 16'bz;  // Controlled_Buffer controlled_buffer_21
  assign out_9 = not_1_out ? controlled_buffer_1_out[11] : 1'bz;  // Controlled_Buffer controlled_buffer_22
  Pull_Resistor pull_resistor_5 (.node(out_9));
  assign out_10 = not_1_out ? controlled_buffer_1_out[10] : 1'bz;  // Controlled_Buffer controlled_buffer_23
  Pull_Resistor #(.pull(1)) pull_resistor_6 (.node(out_10));
  assign out_11 = not_1_out ? controlled_buffer_1_out[9] : 1'bz;  // Controlled_Buffer controlled_buffer_24
  Pull_Resistor pull_resistor_7 (.node(out_11));
  Greather greather_1 (.in_1(A), .in_2(B), .out_3(JGE));  // open: out_4
  Equal equal_1 (.in_1(A), .in_2(B), .out_3(JEQ));
  assign out_12 = not_1_out ? controlled_buffer_1_out[8] : 1'bz;  // Controlled_Buffer controlled_buffer_25
  assign out_13 = not_1_out ? controlled_buffer_1_out[7] : 1'bz;  // Controlled_Buffer controlled_buffer_26
  Pull_Resistor pull_resistor_8 (.node(out_13));
  Pull_Resistor pull_resistor_9 (.node(out_12));
  assign B = G_L ? {8{1'b0}} : 8'bz;  // Controlled_Buffer controlled_buffer_27
  not not_2 (not_2_out, G_L);
  assign A = not_2_out ? {8{1'b0}} : 8'bz;  // Controlled_Buffer controlled_buffer_28
  not not_3 (JLE, JGE);
  not not_4 (JLT, JGE);
  not not_5 (JDZ, JEQ);
  not not_6 (not_6_out, G_L2);
  not not_7 (not_7_out, G_L3);
  nor nor_1 (nor_1_out, G_L0, G_L1, G_L2, G_L3);
  assign out_14 = not_1_out ? controlled_buffer_1_out[6] : 1'bz;  // Controlled_Buffer controlled_buffer_29
  Pull_Resistor pull_resistor_10 (.node(out_14));
  assign B = not_8_out ? in_2[7:0] : 8'bz;  // Controlled_Buffer controlled_buffer_30
  not not_8 (not_8_out, G_L);
  assign A = G_L ? in_2[7:0] : 8'bz;  // Controlled_Buffer controlled_buffer_31
  assign controlled_buffer_32_out = G_L0 ? G_L0 : 1'bz;  // Controlled_Buffer controlled_buffer_32
  assign controlled_buffer_32_out = G_L1 ? G_L1 : 1'bz;  // Controlled_Buffer controlled_buffer_33
  assign controlled_buffer_32_out = G_L2 ? not_6_out : 1'bz;  // Controlled_Buffer controlled_buffer_34
  assign controlled_buffer_32_out = G_L3 ? not_7_out : 1'bz;  // Controlled_Buffer controlled_buffer_35
  assign out_15 = not_1_out ? controlled_buffer_1_out[5] : 1'bz;  // Controlled_Buffer controlled_buffer_36
  Pull_Resistor pull_resistor_11 (.node(out_15));
  or or_1 (G_L, controlled_buffer_32_out, nor_1_out);
  assign out_16 = not_1_out ? controlled_buffer_1_out[4] : 1'bz;  // Controlled_Buffer controlled_buffer_37
  assign out_17 = not_1_out ? controlled_buffer_1_out[3] : 1'bz;  // Controlled_Buffer controlled_buffer_38
  Pull_Resistor pull_resistor_12 (.node(out_16));
  Pull_Resistor pull_resistor_13 (.node(out_17));
  assign out_18[2] = not_1_out ? controlled_buffer_1_out[2] : 1'bz;  // Controlled_Buffer controlled_buffer_39
  Pull_Resistor pull_resistor_14 (.node(out_18[2]));
  assign out_18[1] = not_1_out ? controlled_buffer_1_out[1] : 1'bz;  // Controlled_Buffer controlled_buffer_40
  Pull_Resistor pull_resistor_15 (.node(out_18[1]));
  assign out_18[0] = not_1_out ? controlled_buffer_1_out[0] : 1'bz;  // Controlled_Buffer controlled_buffer_41
  Pull_Resistor pull_resistor_16 (.node(out_18[0]));

  assign out_4 = in_1[7:0];

  // Other names for the same wires on the sheet: JGT = JGE

  // Notes on the sheet:
  //   clock: pull=down
  //   Que significam:
  //   instrução
  //   São 16 bits que irão controlar, respectivamente:
  //   Essas constantes representa a execução da instrução.
  //   RW: Se a RAM estará em modo Read ou Write ( 1 para Read )
  //   endereço
  //   W_ctrl: Se quem vai dizer o proximo endereço para a RAM é o PC ou o Ctrl direto
  //   set_pc: informa o circuito do PC se ele deve ter seu valor mudado pelo controle ou não
  //   clear: informa o flip-flop que cuida do desligamento da CPU se ele deve desliga-lá ou não
  //   R_io, W_io, W_ctrl, RW, R_acc, R_ir, write_acc, set_pc, clear, sel_ACC, open_ALU, R_ACC2, W_ACC2, op1, op2, op3
  //   R_acc: controla o buffer que manda o conteudo da RAM para ACC ( ativado quando ACC deve receber um valor )
  //   R_ir: controla o buffer que manda o countedo da RAM para IR ( ativado quando IR deve receber uma instrução )
  //   write_acc: controla o buffer que manda o conteúdo de ACC para RAM ( ativado se o conteúdo de ACC deve ser escrito na RAM )
  //   0011000001100100
  //   0011000001100010
  //   0011000001100011
  //   0011000001100000
  //   0011000001100001
  //   0001010010000000
  //   0010001000000000
  //   0001010100000000
  //   0011100000010000
  //   Execução
  //   ACC
  //   default:NOP
endmodule

module CPU (
  input  [15:0] in_1,
  output [15:0] out_2,
  output [15:0] out_3,
  output [15:0] out_4,
  output [15:0] out_5,
  output [7:0] out_6,
  output [2:0] out_7,
  output out_8
);

  wire and_1_out, \begin , button_1_out, clear, clock_1_out, clock_2_out, clock_3_out, clock_4_out,
       clock_5_out, clock_6_out, clock_7_out, ctrl_1_out_7, ctrl_1_out_8, ctrl_1_out_9, ctrl_1_out_10,
       ctrl_1_out_11, ctrl_1_out_12, ctrl_1_out_13, ctrl_1_out_14, ctrl_1_out_15, j_k_ff_2_qn, ligado,
       not_1_out, not_2_out, not_3_out, not_4_out, not_5_out, not_6_out, or_1_out, R_acc2, R_io, W_acc2, W_io;
  wire [7:0] controlled_buffer_1_out, ctrl_1_out_4, pc_1_out_5;
  wire [15:0] ALU, controlled_buffer_3_out, controlled_buffer_4_out, controlled_buffer_5_out,
       controlled_buffer_6_out, controlled_buffer_8_out, multiplexer_1_out, multiplexer_2_out, register_1_q,
       register_3_q;

  assign controlled_buffer_1_out = not_2_out ? pc_1_out_5 : 8'bz;  // Controlled_Buffer controlled_buffer_1
  Multiplexer #(.width(16), .enable("false")) multiplexer_1 (
    .in0(out_5), .in1(out_3), .out(multiplexer_1_out), .sel(not_1_out));
  not not_1 (not_1_out, clock_1_out);
  Clock clock_1 (.out(clock_1_out));
  not not_2 (not_2_out, ctrl_1_out_7);
  PC pc_1 (.clear(clear), .clock(and_1_out), .set(ctrl_1_out_12), .in_4(ctrl_1_out_4), .out_5(pc_1_out_5));
  not not_3 (not_3_out, clock_2_out);
  and and_1 (and_1_out, not_3_out, \begin );
  Register #(.width(16), .trigger("high")) register_1 (
    .D(multiplexer_1_out), .en(ligado), .Q(register_1_q), .clk(or_1_out), .clr(clear));
  or or_1 (or_1_out, not_1_out, R_acc2);
  assign controlled_buffer_1_out = ctrl_1_out_7 ? ctrl_1_out_4 : 8'bz;  // Controlled_Buffer controlled_buffer_2
  Clock clock_2 (.out(clock_2_out));
  assign controlled_buffer_3_out = ctrl_1_out_15 ? register_1_q : 16'bz;  // Controlled_Buffer controlled_buffer_3
  assign controlled_buffer_4_out = ctrl_1_out_15 ? out_5 : 16'bz;  // Controlled_Buffer controlled_buffer_4
  not not_4 (not_4_out, clock_3_out);
  Clock clock_3 (.out(clock_3_out));
  not not_5 (not_5_out, clock_4_out);
  Clock clock_4 (.out(clock_4_out));
  ALU alu_1 (.Overflow(out_8), .in_1(controlled_buffer_3_out), .in_2(controlled_buffer_4_out), .out_5(ALU), .Op(out_7));
  assign controlled_buffer_5_out = R_io ? in_1 : 16'bz;  // Controlled_Buffer controlled_buffer_5
  RAM #(.dataWidth(16)) ram_1 (
    .addr(controlled_buffer_1_out), .data(controlled_buffer_5_out), .sel(ligado), .clk(not_4_out),
    .ld(ctrl_1_out_8));  // open: clr
  assign controlled_buffer_6_out = ctrl_1_out_9 ? controlled_buffer_5_out : 16'bz;  // Controlled_Buffer controlled_buffer_6
  Multiplexer #(.width(16), .enable("false")) multiplexer_2 (
    .in0(controlled_buffer_6_out), .in1(ALU), .out(multiplexer_2_out), .sel(ctrl_1_out_14));
  Ctrl ctrl_1 (
    .in_1(register_3_q), .out_4(ctrl_1_out_4), .out_7(ctrl_1_out_7), .out_9(ctrl_1_out_9),
    .out_10(ctrl_1_out_10), .out_11(ctrl_1_out_11), .out_12(ctrl_1_out_12), .out_13(ctrl_1_out_13),
    .out_14(ctrl_1_out_14), .clock(not_5_out), .out_15(ctrl_1_out_15), .out_16(R_acc2), .out_17(W_acc2),
    .out_18(out_7), .in_2(out_3), .out_8(ctrl_1_out_8), .out_5(R_io), .out_6(W_io));
  assign out_2 = W_io ? controlled_buffer_5_out : 16'bz;  // Controlled_Buffer controlled_buffer_7
  assign controlled_buffer_8_out = ctrl_1_out_10 ? controlled_buffer_5_out : 16'bz;  // Controlled_Buffer controlled_buffer_8
  Register #(.width(16), .trigger("high")) register_2 (
    .D(multiplexer_2_out), .en(ligado), .Q(out_3), .clk(clock_5_out), .clr(clear));
  Clock clock_5 (.out(clock_5_out));
  Register #(.width(16), .trigger("high")) register_3 (
    .D(controlled_buffer_8_out), .en(ligado), .Q(register_3_q), .clk(not_6_out), .clr(clear));
  not not_6 (not_6_out, clock_6_out);
  Clock clock_6 (.out(clock_6_out));
  assign controlled_buffer_5_out = ctrl_1_out_11 ? out_3 : 16'bz;  // Controlled_Buffer controlled_buffer_9
  Clock clock_7 (.out(clock_7_out));
  Button button_1 (.out(button_1_out));
  J_K_Flip_Flop j_k_ff_1 (
    .J(1'b1), .clk(clock_7_out), .K(1'b0), .Q(\begin ), .en(ligado), .reset(clear));  // open: Qn, preset
  J_K_Flip_Flop j_k_ff_2 (
    .J(1'b1), .clk(button_1_out), .K(1'b1), .Q(ligado), .Qn(j_k_ff_2_qn), .en(1'b1), .reset(ctrl_1_out_13));  // open: preset
  or or_2 (clear, j_k_ff_2_qn, ctrl_1_out_13);

  // Other names for the same wires on the sheet: A[7:0] = out_6; ACC[15:0] = out_3; D[15:0] = out_5; IR[15:0] = out_4;
  //   op[2:0] = out_7; over = out_8

  // Notes on the sheet:
  //   ACC 2
  //   Para ligar a CPU, pressionar o botao START
  //   R_ir
  //   ACC
  //   IR
  //   Valores:
  //   START
  //   a instrucao STP desliga a CPU
  //   Como o PC se auto-incrementa quando recebe o clock,
  //   esse flip-flop impede que ele faça isso no primeiro pulso.
endmodule

module _2s_complement (
  input  [15:0] in_1,
  output [15:0] out_2,
  output overflow
);

  wire [15:0] not_1_out;

  assign not_1_out = ~in_1;  // NOT_Gate not_1, 16 bits wide
  Adder #(.width(16)) adder_1 (.a(16'h1), .b(not_1_out), .out(out_2), .cout(overflow));  // open: cin
endmodule

module multiplier (
  input  [15:0] A,
  input  [15:0] B,
  output [15:0] produto,
  output overflow
);

  wire [15:0] multiplier_1_cout;

  Multiplier #(.width(16)) multiplier_1 (.a(A), .b(B), .out(produto), .cout(multiplier_1_cout));  // open: cin
  or or_1 (overflow, produto[15], multiplier_1_cout[0], multiplier_1_cout[1], multiplier_1_cout[2], multiplier_1_cout[3], multiplier_1_cout[4], multiplier_1_cout[5], multiplier_1_cout[6], multiplier_1_cout[7], multiplier_1_cout[8], multiplier_1_cout[9], multiplier_1_cout[10], multiplier_1_cout[11], multiplier_1_cout[12], multiplier_1_cout[13], multiplier_1_cout[14], multiplier_1_cout[15]);
endmodule

module divider (
  input  [15:0] A,
  input  [15:0] B,
  output [15:0] Quociente,
  output [15:0] Resto,
  output out_5
);

  wire and_1_out, and_2_out, nor_1_out, nor_2_out;

  Divider #(.width(16)) divider_1 (.a(A), .b(B), .out(Quociente), .upper({16{1'b0}}), .rem(Resto));
  nor nor_1 (nor_1_out, A[0], A[1], A[2], A[3], A[4], A[5], A[6], A[7], A[8], A[9], A[10], A[11], A[12], A[13], A[14]);
  and and_1 (and_1_out, B[0], B[1], B[2], B[3], B[4], B[5], B[6], B[7], B[8], B[9], B[10], B[11], B[12], B[13], B[14], B[15]);
  nor nor_2 (nor_2_out, B[0], B[1], B[2], B[3], B[4], B[5], B[6], B[7], B[8], B[9], B[10], B[11], B[12], B[13], B[14], B[15]);
  and and_2 (and_2_out, nor_1_out, A[15], and_1_out);
  or or_1 (out_5, and_2_out, nor_2_out);

  // Other names for the same wires on the sheet: overflow_A[15:0] = A; overflow_B[15:0] = B
endmodule

module subtractor (
  input  [15:0] A,
  input  [15:0] B,
  output overflow,
  output [15:0] produto
);

  wire [15:0] n2s_complement_1_out_2;

  _2s_complement u_2s_complement_1 (.in_1(B), .out_2(n2s_complement_1_out_2));  // open: overflow
  adder adder_1 (.in_1(A), .in_2(n2s_complement_1_out_2), .out_4(produto), .out_3(overflow));
endmodule

module Greather (
  input  [7:0] in_1,
  input  [7:0] in_2,
  output out_3,
  output out_4
);

  wire [6:0] sub8bit_1_produto;

  sub8bit sub8bit_1 (.A(in_1), .B(in_2), .overflow(out_4), .produto({out_3, sub8bit_1_produto}));
endmodule

module sub8bit (
  input  [7:0] A,
  input  [7:0] B,
  output [7:0] produto,
  output overflow
);

  wire [7:0] n2comp_8bit_1_out_2;

  _2comp_8bit u_2comp_8bit_1 (.in_1(B), .out_2(n2comp_8bit_1_out_2));  // open: overflow
  Adder adder_1 (.a(A), .b(n2comp_8bit_1_out_2), .out(produto), .cout(overflow));  // open: cin
endmodule

module _2comp_8bit (
  input  [7:0] in_1,
  output [7:0] out_2,
  output overflow
);

  wire [7:0] not_1_out;

  assign not_1_out = ~in_1;  // NOT_Gate not_1, 8 bits wide
  Adder adder_1 (.a(8'h1), .b(not_1_out), .out(out_2), .cout(overflow));  // open: cin
endmodule

module Equal (
  input  [7:0] in_1,
  input  [7:0] in_2,
  output out_3
);

  wire xnor_1_out, xnor_2_out, xnor_3_out, xnor_4_out, xnor_5_out, xnor_6_out, xnor_7_out, xnor_8_out;

  xnor xnor_1 (xnor_1_out, in_2[0], in_1[0]);
  xnor xnor_2 (xnor_2_out, in_1[1], in_2[1]);
  xnor xnor_3 (xnor_3_out, in_1[2], in_2[2]);
  xnor xnor_4 (xnor_4_out, in_1[3], in_2[3]);
  xnor xnor_5 (xnor_5_out, in_1[4], in_2[4]);
  xnor xnor_6 (xnor_6_out, in_1[5], in_2[5]);
  xnor xnor_7 (xnor_7_out, in_1[6], in_2[6]);
  xnor xnor_8 (xnor_8_out, in_1[7], in_2[7]);
  and and_1 (out_3, xnor_1_out, xnor_2_out, xnor_3_out, xnor_4_out, xnor_5_out, xnor_6_out, xnor_7_out, xnor_8_out);

  // Other names for the same wires on the sheet: _0 = in_2[0]; _1 = in_2[1]; _2 = in_2[2]; _3 = in_2[3]; _4 = in_2[4];
  //   _5 = in_2[5]; _6 = in_2[6]; _7 = in_2[7]
endmodule

module adder (
  input  [15:0] in_1,
  input  [15:0] in_2,
  output out_3,
  output [15:0] out_4
);

  wire fulladder_1_ci_1, fulladder_2_ci_1, fulladder_3_ci_1, fulladder_4_ci_1, fulladder_5_ci_1,
       fulladder_6_ci_1, fulladder_7_ci_1, fulladder_8_ci_1, fulladder_9_ci_1, fulladder_10_ci_1,
       fulladder_11_ci_1, fulladder_12_ci_1, fulladder_13_ci_1, fulladder_14_ci_1, fulladder_15_ci_1,
       halfadder_1_carry;

  xor xor_1 (out_3, fulladder_2_ci_1, fulladder_1_ci_1);
  FullAdder fulladder_1 (.AI(in_1[15]), .BI(in_2[15]), .CI(fulladder_2_ci_1), .SUM(out_4[15]), .CI_1(fulladder_1_ci_1));
  Pull_Resistor pull_resistor_1 (.node(in_1[14]));
  Pull_Resistor pull_resistor_2 (.node(in_1[15]));
  Pull_Resistor pull_resistor_3 (.node(in_1[13]));
  FullAdder fulladder_2 (.AI(in_1[14]), .BI(in_2[14]), .CI(fulladder_3_ci_1), .SUM(out_4[14]), .CI_1(fulladder_2_ci_1));
  Pull_Resistor pull_resistor_4 (.node(in_1[12]));
  Pull_Resistor pull_resistor_5 (.node(in_1[11]));
  FullAdder fulladder_3 (.AI(in_1[13]), .BI(in_2[13]), .CI(fulladder_4_ci_1), .SUM(out_4[13]), .CI_1(fulladder_3_ci_1));
  Pull_Resistor pull_resistor_6 (.node(in_1[10]));
  Pull_Resistor pull_resistor_7 (.node(in_1[9]));
  Pull_Resistor pull_resistor_8 (.node(in_1[8]));
  FullAdder fulladder_4 (.AI(in_1[12]), .BI(in_2[12]), .CI(fulladder_5_ci_1), .SUM(out_4[12]), .CI_1(fulladder_4_ci_1));
  Pull_Resistor pull_resistor_9 (.node(in_1[6]));
  Pull_Resistor pull_resistor_10 (.node(in_1[7]));
  FullAdder fulladder_5 (.AI(in_1[11]), .BI(in_2[11]), .CI(fulladder_6_ci_1), .SUM(out_4[11]), .CI_1(fulladder_5_ci_1));
  Pull_Resistor pull_resistor_11 (.node(in_1[5]));
  Pull_Resistor pull_resistor_12 (.node(in_1[4]));
  Pull_Resistor pull_resistor_13 (.node(in_1[3]));
  FullAdder fulladder_6 (.AI(in_1[10]), .BI(in_2[10]), .CI(fulladder_7_ci_1), .SUM(out_4[10]), .CI_1(fulladder_6_ci_1));
  Pull_Resistor pull_resistor_14 (.node(in_1[2]));
  FullAdder fulladder_7 (.AI(in_1[9]), .BI(in_2[9]), .CI(fulladder_8_ci_1), .SUM(out_4[9]), .CI_1(fulladder_7_ci_1));
  Pull_Resistor pull_resistor_15 (.node(in_1[1]));
  Pull_Resistor pull_resistor_16 (.node(in_1[0]));
  Pull_Resistor pull_resistor_17 (.node(in_2[15]));
  FullAdder fulladder_8 (.AI(in_1[8]), .BI(in_2[8]), .CI(fulladder_9_ci_1), .SUM(out_4[8]), .CI_1(fulladder_8_ci_1));
  Pull_Resistor pull_resistor_18 (.node(in_2[14]));
  Pull_Resistor pull_resistor_19 (.node(in_2[13]));
  FullAdder fulladder_9 (.AI(in_1[7]), .BI(in_2[7]), .CI(fulladder_10_ci_1), .SUM(out_4[7]), .CI_1(fulladder_9_ci_1));
  Pull_Resistor pull_resistor_20 (.node(in_2[12]));
  Pull_Resistor pull_resistor_21 (.node(in_2[11]));
  Pull_Resistor pull_resistor_22 (.node(in_2[10]));
  FullAdder fulladder_10 (.AI(in_1[6]), .BI(in_2[6]), .CI(fulladder_11_ci_1), .SUM(out_4[6]), .CI_1(fulladder_10_ci_1));
  Pull_Resistor pull_resistor_23 (.node(in_2[8]));
  Pull_Resistor pull_resistor_24 (.node(in_2[9]));
  FullAdder fulladder_11 (.AI(in_1[5]), .BI(in_2[5]), .CI(fulladder_12_ci_1), .SUM(out_4[5]), .CI_1(fulladder_11_ci_1));
  Pull_Resistor pull_resistor_25 (.node(in_2[7]));
  Pull_Resistor pull_resistor_26 (.node(in_2[6]));
  Pull_Resistor pull_resistor_27 (.node(in_2[5]));
  FullAdder fulladder_12 (.AI(in_1[4]), .BI(in_2[4]), .CI(fulladder_13_ci_1), .SUM(out_4[4]), .CI_1(fulladder_12_ci_1));
  Pull_Resistor pull_resistor_28 (.node(in_2[3]));
  Pull_Resistor pull_resistor_29 (.node(in_2[4]));
  FullAdder fulladder_13 (.AI(in_1[3]), .BI(in_2[3]), .CI(fulladder_14_ci_1), .SUM(out_4[3]), .CI_1(fulladder_13_ci_1));
  Pull_Resistor pull_resistor_30 (.node(in_2[2]));
  Pull_Resistor pull_resistor_31 (.node(in_2[0]));
  Pull_Resistor pull_resistor_32 (.node(in_2[1]));
  FullAdder fulladder_14 (.AI(in_1[2]), .BI(in_2[2]), .CI(fulladder_15_ci_1), .SUM(out_4[2]), .CI_1(fulladder_14_ci_1));
  FullAdder fulladder_15 (.AI(in_1[1]), .BI(in_2[1]), .CI(halfadder_1_carry), .SUM(out_4[1]), .CI_1(fulladder_15_ci_1));
  HalfAdder halfadder_1 (.AI(in_1[0]), .BI(in_2[0]), .SUM(out_4[0]), .Carry(halfadder_1_carry));

  // Other names for the same wires on the sheet: a0 = in_1[0]; a1 = in_1[1]; a2 = in_1[2]; a3 = in_1[3]; a4 = in_1[4];
  //   a5 = in_1[5]; a6 = in_1[6]; a7 = in_1[7]; a8 = in_1[8]; a9 = in_1[9]; a10 = in_1[10]; a11 = in_1[11];
  //   a12 = in_1[12]; a13 = in_1[13]; a14 = in_1[14]; a15 = in_1[15]; b0 = in_2[0]; b1 = in_2[1]; b2 = in_2[2];
  //   b3 = in_2[3]; b4 = in_2[4]; b5 = in_2[5]; b6 = in_2[6]; b7 = in_2[7]; b8 = in_2[8]; b9 = in_2[9];
  //   b10 = in_2[10]; b11 = in_2[11]; b12 = in_2[12]; b13 = in_2[13]; b14 = in_2[14]; b15 = in_2[15]
endmodule

module HalfAdder (
  input  AI,
  input  BI,
  output SUM,
  output Carry
);

  xor xor_1 (SUM, AI, BI);
  and and_1 (Carry, AI, BI);
endmodule

module FullAdder (
  input  AI,
  input  BI,
  input  CI,
  output SUM,
  output CI_1
);

  wire and_1_out, and_2_out, xor_1_out;

  xor xor_1 (xor_1_out, AI, BI);
  and and_1 (and_1_out, AI, BI);
  and and_2 (and_2_out, xor_1_out, CI);
  xor xor_2 (SUM, xor_1_out, CI);
  or or_1 (CI_1, and_1_out, and_2_out);
endmodule
