// Logisim project ALU.circ as structural Verilog: 18 circuits, main circuit ALU
module HalfAdder (
  input  AI,
  input  BI,
  output SUM,
  output Carry
);

  xor xor_1 (SUM, AI, BI);
  and and_1 (Carry, AI, BI);
endmodule

module FullAdder (
  input  AI,
  input  BI,
  input  CI,
  output SUM,
  output CI_1
);

  wire and_1_out, and_2_out, xor_1_out;

  xor xor_1 (xor_1_out, AI, BI);
  and and_1 (and_1_out, AI, BI);
  and and_2 (and_2_out, xor_1_out, CI);
  xor xor_2 (SUM, xor_1_out, CI);
  or or_1 (CI_1, and_1_out, and_2_out);
endmodule

module _8bitAdder (
  input  a7,
  input  in_2,
  input  a6,
  input  in_4,
  input  a5,
  input  in_6,
  input  a4,
  input  in_8,
  input  a3,
  input  in_10,
  input  a2,
  input  in_12,
  input  a1,
  input  b1,
  input  a0,
  input  b0,
  output out_17,
  output out_18,
  output out_19,
  output out_20,
  output out_21,
  output out_22,
  output out_23,
  output out_24,
  output Overflow
);

  wire fulladder_1_ci_1, fulladder_2_ci_1, fulladder_3_ci_1, fulladder_4_ci_1, fulladder_5_ci_1,
       fulladder_6_ci_1, fulladder_7_ci_1, halfadder_1_carry;

  xor xor_1 (Overflow, fulladder_2_ci_1, fulladder_1_ci_1);
  FullAdder fulladder_1 (.AI(a7), .BI(in_2), .CI(fulladder_2_ci_1), .SUM(out_17), .CI_1(fulladder_1_ci_1));
  FullAdder fulladder_2 (.AI(a6), .BI(in_4), .CI(fulladder_3_ci_1), .SUM(out_18), .CI_1(fulladder_2_ci_1));
  FullAdder fulladder_3 (.AI(a5), .BI(in_6), .CI(fulladder_4_ci_1), .SUM(out_19), .CI_1(fulladder_3_ci_1));
  FullAdder fulladder_4 (.AI(a4), .BI(in_8), .CI(fulladder_5_ci_1), .SUM(out_20), .CI_1(fulladder_4_ci_1));
  FullAdder fulladder_5 (.AI(a3), .BI(in_10), .CI(fulladder_6_ci_1), .SUM(out_21), .CI_1(fulladder_5_ci_1));
  FullAdder fulladder_6 (.AI(a2), .BI(in_12), .CI(fulladder_7_ci_1), .SUM(out_22), .CI_1(fulladder_6_ci_1));
  FullAdder fulladder_7 (.AI(a1), .BI(b1), .CI(halfadder_1_carry), .SUM(out_23), .CI_1(fulladder_7_ci_1));
  HalfAdder halfadder_1 (.AI(a0), .BI(b0), .SUM(out_24), .Carry(halfadder_1_carry));
endmodule

module _8Adder (
  input  [7:0] in_1,
  input  [7:0] in_2,
  output overflow,
  output [7:0] out_4
);

  _8bitAdder u_8bitadder_1 (
    .out_24(out_4[0]), .a0(in_1[0]), .b0(in_2[0]), .a1(in_1[1]), .b1(in_2[1]), .a2(in_1[2]), .in_12(in_2[2]),
    .a3(in_1[3]), .in_10(in_2[3]), .a4(in_1[4]), .in_8(in_2[4]), .a5(in_1[5]), .in_6(in_2[5]), .a6(in_1[6]),
    .in_4(in_2[6]), .a7(in_1[7]), .in_2(in_2[7]), .out_23(out_4[1]), .out_22(out_4[2]), .out_18(out_4[6]),
    .out_17(out_4[7]), .Overflow(overflow), .out_19(out_4[5]), .out_20(out_4[4]), .out_21(out_4[3]));
endmodule

module complemento2 (
  input  [7:0] in_1,
  output [7:0] out_2
);

  wire [7:0] not_1_out;

  assign not_1_out = ~in_1;  // NOT_Gate not_1, 8 bits wide
  _8Adder u_8adder_1 (.in_1(8'h1), .in_2(not_1_out), .out_4(out_2));  // open: overflow
endmodule

module _8Subtracter (
  input  [7:0] in_1,
  input  [7:0] in_2,
  output out_3,
  output [7:0] out_4
);

  wire [7:0] complemento2_1_out_2;

  complemento2 complemento2_1 (.in_1(in_2), .out_2(complemento2_1_out_2));
  _8Adder u_8adder_1 (.in_1(in_1), .in_2(complemento2_1_out_2), .out_4(out_4), .overflow(out_3));

  // Notes on the sheet:
  //   overflow
endmodule

module _8bitMultiplier (
  input  in_1,
  input  in_2,
  input  in_3,
  input  in_4,
  input  in_5,
  input  in_6,
  input  in_7,
  input  x0,
  input  y0,
  input  in_10,
  input  in_11,
  input  in_12,
  input  in_13,
  input  in_14,
  input  in_15,
  input  in_16,
  output out_17,
  output out_18,
  output out_19,
  output out_20,
  output out_21,
  output out_22,
  output out_23,
  output out_24,
  output out_25
);

  wire and_1_out, and_2_out, and_3_out, and_4_out, and_5_out, and_6_out, and_7_out, and_8_out, and_9_out,
       and_10_out, and_11_out, and_12_out, and_13_out, and_14_out, and_15_out, and_16_out, and_17_out,
       and_18_out, and_19_out, and_20_out, and_21_out, and_22_out, and_23_out, and_24_out, and_25_out,
       and_26_out, and_27_out, and_28_out, and_29_out, and_30_out, and_31_out, and_32_out, and_33_out,
       and_34_out, and_35_out, and_36_out, and_37_out, and_38_out, and_39_out, and_40_out, and_41_out,
       and_42_out, and_43_out, and_44_out, and_45_out, and_46_out, and_47_out, and_48_out, and_49_out,
       and_50_out, and_51_out, and_52_out, and_53_out, and_54_out, and_55_out, and_56_out, and_57_out,
       and_58_out, and_59_out, and_60_out, and_61_out, and_62_out, and_63_out, fulladder_1_ci_1,
       fulladder_1_sum, fulladder_2_ci_1, fulladder_2_sum, fulladder_3_ci_1, fulladder_3_sum,
       fulladder_4_ci_1, fulladder_4_sum, fulladder_5_ci_1, fulladder_5_sum, fulladder_6_ci_1,
       fulladder_6_sum, fulladder_7_ci_1, fulladder_7_sum, fulladder_8_ci_1, fulladder_8_sum,
       fulladder_9_ci_1, fulladder_9_sum, fulladder_10_ci_1, fulladder_10_sum, fulladder_11_ci_1,
       fulladder_11_sum, fulladder_12_ci_1, fulladder_12_sum, fulladder_13_ci_1, fulladder_13_sum,
       fulladder_14_ci_1, fulladder_14_sum, fulladder_15_ci_1, fulladder_15_sum, fulladder_16_ci_1,
       fulladder_16_sum, fulladder_17_ci_1, fulladder_17_sum, fulladder_18_ci_1, fulladder_18_sum,
       fulladder_19_ci_1, fulladder_19_sum, fulladder_20_ci_1, fulladder_20_sum, fulladder_21_ci_1,
       fulladder_21_sum, fulladder_22_ci_1, fulladder_22_sum, fulladder_23_ci_1, fulladder_23_sum,
       fulladder_24_ci_1, fulladder_24_sum, fulladder_25_ci_1, fulladder_25_sum, fulladder_26_ci_1,
       fulladder_26_sum, fulladder_27_ci_1, fulladder_27_sum, fulladder_28_ci_1, fulladder_28_sum,
       fulladder_29_ci_1, fulladder_29_sum, fulladder_30_ci_1, fulladder_30_sum, fulladder_31_ci_1,
       fulladder_31_sum, fulladder_32_ci_1, fulladder_32_sum, fulladder_33_ci_1, fulladder_33_sum,
       fulladder_34_ci_1, fulladder_34_sum, fulladder_35_ci_1, fulladder_35_sum, fulladder_36_ci_1,
       fulladder_36_sum, fulladder_37_ci_1, fulladder_37_sum, fulladder_38_ci_1, fulladder_38_sum,
       fulladder_39_ci_1, fulladder_39_sum, fulladder_40_ci_1, fulladder_40_sum, fulladder_41_ci_1,
       fulladder_41_sum, fulladder_42_ci_1, fulladder_42_sum, fulladder_43_ci_1, fulladder_43_sum,
       fulladder_44_ci_1, fulladder_44_sum, fulladder_45_ci_1, fulladder_45_sum, fulladder_46_ci_1,
       fulladder_46_sum, fulladder_47_ci_1, fulladder_47_sum, fulladder_48_ci_1, fulladder_48_sum,
       fulladder_49_ci_1, fulladder_49_sum, halfadder_1_sum, halfadder_2_carry, halfadder_3_carry,
       halfadder_4_carry, halfadder_5_carry, halfadder_6_carry, halfadder_7_carry, halfadder_8_carry,
       not_1_out, not_2_out, not_3_out, not_4_out, not_5_out, not_6_out, not_7_out, not_8_out, not_9_out,
       not_10_out, not_11_out, not_12_out, not_13_out, not_14_out, xor_1_out, xor_2_out, xor_3_out,
       xor_4_out, xor_5_out, xor_6_out, xor_7_out, xor_8_out;

  HalfAdder halfadder_1 (.AI(1'b1), .BI(fulladder_1_ci_1), .SUM(halfadder_1_sum));  // open: Carry
  xor xor_1 (xor_1_out, halfadder_1_sum, fulladder_1_sum);
  FullAdder fulladder_1 (
    .AI(fulladder_2_ci_1), .BI(and_1_out), .CI(fulladder_3_ci_1), .SUM(fulladder_1_sum),
    .CI_1(fulladder_1_ci_1));
  xor xor_2 (xor_2_out, fulladder_1_sum, fulladder_3_sum);
  and and_1 (and_1_out, in_1, in_16);
  and and_2 (and_2_out, in_1, in_15);
  not not_1 (not_1_out, and_2_out);
  FullAdder fulladder_2 (
    .AI(fulladder_4_ci_1), .BI(not_1_out), .CI(fulladder_5_ci_1), .SUM(fulladder_2_sum),
    .CI_1(fulladder_2_ci_1));
  and and_3 (and_3_out, in_2, in_16);
  not not_2 (not_2_out, and_3_out);
  FullAdder fulladder_3 (
    .AI(fulladder_2_sum), .BI(not_2_out), .CI(fulladder_6_ci_1), .SUM(fulladder_3_sum),
    .CI_1(fulladder_3_ci_1));
  xor xor_3 (xor_3_out, fulladder_3_sum, fulladder_6_sum);
  and and_4 (and_4_out, in_1, in_14);
  not not_3 (not_3_out, and_4_out);
  FullAdder fulladder_4 (
    .AI(fulladder_7_ci_1), .BI(not_3_out), .CI(fulladder_8_ci_1), .SUM(fulladder_4_sum),
    .CI_1(fulladder_4_ci_1));
  and and_5 (and_5_out, in_2, in_15);
  FullAdder fulladder_5 (
    .AI(fulladder_4_sum), .BI(and_5_out), .CI(fulladder_10_ci_1), .SUM(fulladder_5_sum),
    .CI_1(fulladder_5_ci_1));
  FullAdder fulladder_6 (
    .AI(fulladder_5_sum), .BI(not_5_out), .CI(fulladder_11_ci_1), .SUM(fulladder_6_sum),
    .CI_1(fulladder_6_ci_1));
  xor xor_4 (xor_4_out, fulladder_6_sum, fulladder_11_sum);
  and and_6 (and_6_out, in_1, in_13);
  not not_4 (not_4_out, and_6_out);
  FullAdder fulladder_7 (
    .AI(fulladder_9_ci_1), .BI(not_4_out), .CI(fulladder_12_ci_1), .SUM(fulladder_7_sum),
    .CI_1(fulladder_7_ci_1));
  FullAdder fulladder_8 (
    .AI(fulladder_7_sum), .BI(and_8_out), .CI(fulladder_13_ci_1), .SUM(fulladder_8_sum),
    .CI_1(fulladder_8_ci_1));
  and and_7 (and_7_out, in_3, in_16);
  not not_5 (not_5_out, and_7_out);
  FullAdder fulladder_9 (
    .AI(fulladder_16_ci_1), .BI(not_7_out), .CI(fulladder_17_ci_1), .SUM(fulladder_9_sum),
    .CI_1(fulladder_9_ci_1));
  and and_8 (and_8_out, in_2, in_14);
  and and_9 (and_9_out, in_3, in_15);
  FullAdder fulladder_10 (
    .AI(fulladder_8_sum), .BI(and_9_out), .CI(fulladder_14_ci_1), .SUM(fulladder_10_sum),
    .CI_1(fulladder_10_ci_1));
  and and_10 (and_10_out, in_4, in_16);
  not not_6 (not_6_out, and_10_out);
  FullAdder fulladder_11 (
    .AI(fulladder_10_sum), .BI(not_6_out), .CI(fulladder_15_ci_1), .SUM(fulladder_11_sum),
    .CI_1(fulladder_11_ci_1));
  xor xor_5 (xor_5_out, fulladder_11_sum, fulladder_15_sum);
  or or_1 (out_25, xor_1_out, xor_2_out, xor_3_out, xor_4_out, xor_5_out, xor_6_out, xor_7_out, xor_8_out);
  and and_11 (and_11_out, in_1, in_12);
  not not_7 (not_7_out, and_11_out);
  and and_12 (and_12_out, in_2, in_13);
  FullAdder fulladder_12 (
    .AI(fulladder_9_sum), .BI(and_12_out), .CI(fulladder_18_ci_1), .SUM(fulladder_12_sum),
    .CI_1(fulladder_12_ci_1));
  and and_13 (and_13_out, in_3, in_14);
  FullAdder fulladder_13 (
    .AI(fulladder_12_sum), .BI(and_13_out), .CI(fulladder_19_ci_1), .SUM(fulladder_13_sum),
    .CI_1(fulladder_13_ci_1));
  and and_14 (and_14_out, in_4, in_15);
  FullAdder fulladder_14 (
    .AI(fulladder_13_sum), .BI(and_14_out), .CI(fulladder_23_ci_1), .SUM(fulladder_14_sum),
    .CI_1(fulladder_14_ci_1));
  FullAdder fulladder_15 (
    .AI(fulladder_14_sum), .BI(not_9_out), .CI(fulladder_24_ci_1), .SUM(fulladder_15_sum),
    .CI_1(fulladder_15_ci_1));
  xor xor_6 (xor_6_out, fulladder_15_sum, fulladder_24_sum);
  and and_15 (and_15_out, in_1, in_11);
  not not_8 (not_8_out, and_15_out);
  FullAdder fulladder_16 (
    .AI(fulladder_20_ci_1), .BI(not_8_out), .CI(fulladder_21_ci_1), .SUM(fulladder_16_sum),
    .CI_1(fulladder_16_ci_1));
  and and_16 (and_16_out, in_2, in_12);
  FullAdder fulladder_17 (
    .AI(fulladder_16_sum), .BI(and_16_out), .CI(fulladder_22_ci_1), .SUM(fulladder_17_sum),
    .CI_1(fulladder_17_ci_1));
  and and_17 (and_17_out, in_3, in_13);
  FullAdder fulladder_18 (
    .AI(fulladder_17_sum), .BI(and_17_out), .CI(fulladder_26_ci_1), .SUM(fulladder_18_sum),
    .CI_1(fulladder_18_ci_1));
  FullAdder fulladder_19 (
    .AI(fulladder_18_sum), .BI(and_21_out), .CI(fulladder_27_ci_1), .SUM(fulladder_19_sum),
    .CI_1(fulladder_19_ci_1));
  and and_18 (and_18_out, in_5, in_16);
  not not_9 (not_9_out, and_18_out);
  and and_19 (and_19_out, in_1, in_10);
  not not_10 (not_10_out, and_19_out);
  FullAdder fulladder_20 (
    .AI(1'b1), .BI(not_10_out), .CI(fulladder_25_ci_1), .SUM(fulladder_20_sum), .CI_1(fulladder_20_ci_1));
  and and_20 (and_20_out, in_2, in_11);
  FullAdder fulladder_21 (
    .AI(fulladder_20_sum), .BI(and_20_out), .CI(fulladder_30_ci_1), .SUM(fulladder_21_sum),
    .CI_1(fulladder_21_ci_1));
  FullAdder fulladder_22 (
    .AI(fulladder_21_sum), .BI(and_25_out), .CI(fulladder_31_ci_1), .SUM(fulladder_22_sum),
    .CI_1(fulladder_22_ci_1));
  and and_21 (and_21_out, in_4, in_14);
  and and_22 (and_22_out, in_5, in_15);
  FullAdder fulladder_23 (
    .AI(fulladder_19_sum), .BI(and_22_out), .CI(fulladder_28_ci_1), .SUM(fulladder_23_sum),
    .CI_1(fulladder_23_ci_1));
  and and_23 (and_23_out, in_14, in_16);
  not not_11 (not_11_out, and_23_out);
  FullAdder fulladder_24 (
    .AI(fulladder_23_sum), .BI(not_11_out), .CI(fulladder_29_ci_1), .SUM(fulladder_24_sum),
    .CI_1(fulladder_24_ci_1));
  xor xor_7 (xor_7_out, fulladder_24_sum, fulladder_29_sum);
  and and_24 (and_24_out, in_1, y0);
  not not_12 (not_12_out, and_24_out);
  FullAdder fulladder_25 (
    .AI(not_12_out), .BI(and_29_out), .CI(fulladder_34_ci_1), .SUM(fulladder_25_sum), .CI_1(fulladder_25_ci_1));
  and and_25 (and_25_out, in_3, in_12);
  and and_26 (and_26_out, in_4, in_13);
  FullAdder fulladder_26 (
    .AI(fulladder_22_sum), .BI(and_26_out), .CI(fulladder_32_ci_1), .SUM(fulladder_26_sum),
    .CI_1(fulladder_26_ci_1));
  and and_27 (and_27_out, in_5, in_14);
  FullAdder fulladder_27 (
    .AI(fulladder_26_sum), .BI(and_27_out), .CI(fulladder_33_ci_1), .SUM(fulladder_27_sum),
    .CI_1(fulladder_27_ci_1));
  and and_28 (and_28_out, in_14, in_15);
  FullAdder fulladder_28 (
    .AI(fulladder_27_sum), .BI(and_28_out), .CI(fulladder_37_ci_1), .SUM(fulladder_28_sum),
    .CI_1(fulladder_28_ci_1));
  FullAdder fulladder_29 (
    .AI(fulladder_28_sum), .BI(not_13_out), .CI(halfadder_2_carry), .SUM(fulladder_29_sum),
    .CI_1(fulladder_29_ci_1));
  xor xor_8 (xor_8_out, fulladder_29_sum, out_24);
  and and_29 (and_29_out, in_2, in_10);
  and and_30 (and_30_out, in_3, in_11);
  FullAdder fulladder_30 (
    .AI(fulladder_25_sum), .BI(and_30_out), .CI(fulladder_35_ci_1), .SUM(fulladder_30_sum),
    .CI_1(fulladder_30_ci_1));
  and and_31 (and_31_out, in_4, in_12);
  FullAdder fulladder_31 (
    .AI(fulladder_30_sum), .BI(and_31_out), .CI(fulladder_36_ci_1), .SUM(fulladder_31_sum),
    .CI_1(fulladder_31_ci_1));
  and and_32 (and_32_out, in_5, in_13);
  FullAdder fulladder_32 (
    .AI(fulladder_31_sum), .BI(and_32_out), .CI(fulladder_39_ci_1), .SUM(fulladder_32_sum),
    .CI_1(fulladder_32_ci_1));
  FullAdder fulladder_33 (
    .AI(fulladder_32_sum), .BI(and_37_out), .CI(fulladder_40_ci_1), .SUM(fulladder_33_sum),
    .CI_1(fulladder_33_ci_1));
  and and_33 (and_33_out, in_7, in_16);
  not not_13 (not_13_out, and_33_out);
  and and_34 (and_34_out, in_2, y0);
  and and_35 (and_35_out, in_3, in_10);
  FullAdder fulladder_34 (
    .AI(and_34_out), .BI(and_35_out), .CI(fulladder_38_ci_1), .SUM(fulladder_34_sum), .CI_1(fulladder_34_ci_1));
  and and_36 (and_36_out, in_4, in_11);
  FullAdder fulladder_35 (
    .AI(fulladder_34_sum), .BI(and_36_out), .CI(fulladder_41_ci_1), .SUM(fulladder_35_sum),
    .CI_1(fulladder_35_ci_1));
  FullAdder fulladder_36 (
    .AI(fulladder_35_sum), .BI(and_41_out), .CI(fulladder_42_ci_1), .SUM(fulladder_36_sum),
    .CI_1(fulladder_36_ci_1));
  and and_37 (and_37_out, in_6, in_14);
  and and_38 (and_38_out, in_7, in_15);
  FullAdder fulladder_37 (
    .AI(fulladder_33_sum), .BI(and_38_out), .CI(halfadder_3_carry), .SUM(fulladder_37_sum),
    .CI_1(fulladder_37_ci_1));
  and and_39 (and_39_out, x0, in_16);
  not not_14 (not_14_out, and_39_out);
  HalfAdder halfadder_2 (.AI(fulladder_37_sum), .BI(not_14_out), .SUM(out_24), .Carry(halfadder_2_carry));
  and and_40 (and_40_out, in_3, y0);
  FullAdder fulladder_38 (
    .AI(and_40_out), .BI(and_45_out), .CI(fulladder_44_ci_1), .SUM(fulladder_38_sum), .CI_1(fulladder_38_ci_1));
  and and_41 (and_41_out, in_5, in_12);
  and and_42 (and_42_out, in_6, in_13);
  FullAdder fulladder_39 (
    .AI(fulladder_36_sum), .BI(and_42_out), .CI(fulladder_43_ci_1), .SUM(fulladder_39_sum),
    .CI_1(fulladder_39_ci_1));
  and and_43 (and_43_out, in_7, in_14);
  FullAdder fulladder_40 (
    .AI(fulladder_39_sum), .BI(and_43_out), .CI(halfadder_4_carry), .SUM(fulladder_40_sum),
    .CI_1(fulladder_40_ci_1));
  and and_44 (and_44_out, x0, in_15);
  HalfAdder halfadder_3 (.AI(fulladder_40_sum), .BI(and_44_out), .SUM(out_17), .Carry(halfadder_3_carry));
  and and_45 (and_45_out, in_4, in_10);
  and and_46 (and_46_out, in_5, in_11);
  FullAdder fulladder_41 (
    .AI(fulladder_38_sum), .BI(and_46_out), .CI(fulladder_45_ci_1), .SUM(fulladder_41_sum),
    .CI_1(fulladder_41_ci_1));
  and and_47 (and_47_out, in_6, in_12);
  FullAdder fulladder_42 (
    .AI(fulladder_41_sum), .BI(and_47_out), .CI(fulladder_46_ci_1), .SUM(fulladder_42_sum),
    .CI_1(fulladder_42_ci_1));
  and and_48 (and_48_out, in_7, in_13);
  FullAdder fulladder_43 (
    .AI(fulladder_42_sum), .BI(and_48_out), .CI(halfadder_5_carry), .SUM(fulladder_43_sum),
    .CI_1(fulladder_43_ci_1));
  HalfAdder halfadder_4 (.AI(fulladder_43_sum), .BI(and_52_out), .SUM(out_18), .Carry(halfadder_4_carry));
  and and_49 (and_49_out, in_4, y0);
  and and_50 (and_50_out, in_5, in_10);
  FullAdder fulladder_44 (
    .AI(and_49_out), .BI(and_50_out), .CI(fulladder_47_ci_1), .SUM(fulladder_44_sum), .CI_1(fulladder_44_ci_1));
  and and_51 (and_51_out, in_6, in_11);
  FullAdder fulladder_45 (
    .AI(fulladder_44_sum), .BI(and_51_out), .CI(fulladder_48_ci_1), .SUM(fulladder_45_sum),
    .CI_1(fulladder_45_ci_1));
  FullAdder fulladder_46 (
    .AI(fulladder_45_sum), .BI(and_54_out), .CI(halfadder_6_carry), .SUM(fulladder_46_sum),
    .CI_1(fulladder_46_ci_1));
  and and_52 (and_52_out, x0, in_14);
  and and_53 (and_53_out, in_5, y0);
  FullAdder fulladder_47 (
    .AI(and_53_out), .BI(and_56_out), .CI(fulladder_49_ci_1), .SUM(fulladder_47_sum), .CI_1(fulladder_47_ci_1));
  and and_54 (and_54_out, in_7, in_12);
  and and_55 (and_55_out, x0, in_13);
  HalfAdder halfadder_5 (.AI(fulladder_46_sum), .BI(and_55_out), .SUM(out_19), .Carry(halfadder_5_carry));
  and and_56 (and_56_out, in_6, in_10);
  and and_57 (and_57_out, in_7, in_11);
  FullAdder fulladder_48 (
    .AI(fulladder_47_sum), .BI(and_57_out), .CI(halfadder_7_carry), .SUM(fulladder_48_sum),
    .CI_1(fulladder_48_ci_1));
  and and_58 (and_58_out, x0, in_12);
  HalfAdder halfadder_6 (.AI(fulladder_48_sum), .BI(and_58_out), .SUM(out_20), .Carry(halfadder_6_carry));
  and and_59 (and_59_out, in_6, y0);
  and and_60 (and_60_out, in_7, in_10);
  FullAdder fulladder_49 (
    .AI(and_59_out), .BI(and_60_out), .CI(halfadder_8_carry), .SUM(fulladder_49_sum), .CI_1(fulladder_49_ci_1));
  and and_61 (and_61_out, x0, in_11);
  HalfAdder halfadder_7 (.AI(fulladder_49_sum), .BI(and_61_out), .SUM(out_21), .Carry(halfadder_7_carry));
  and and_62 (and_62_out, in_7, y0);
  HalfAdder halfadder_8 (.AI(and_62_out), .BI(and_63_out), .SUM(out_22), .Carry(halfadder_8_carry));
  and and_63 (and_63_out, x0, in_10);
  and and_64 (out_23, x0, y0);
endmodule

module _8Multiplier (
  input  [7:0] in_1,
  input  [7:0] in_2,
  output out_3,
  output [7:0] out_4
);

  _8bitMultiplier u_8bitmultiplier_1 (
    .y0(in_2[0]), .in_10(in_2[1]), .in_11(in_2[2]), .in_12(in_2[3]), .in_13(in_2[4]), .in_14(in_2[5]),
    .in_15(in_2[6]), .in_16(in_2[7]), .in_1(in_1[7]), .in_2(in_1[6]), .in_3(in_1[5]), .in_4(in_1[4]),
    .in_5(in_1[3]), .in_6(in_1[2]), .in_7(in_1[1]), .x0(in_1[0]), .out_25(out_3), .out_17(out_4[6]),
    .out_18(out_4[5]), .out_19(out_4[4]), .out_20(out_4[3]), .out_21(out_4[2]), .out_22(out_4[1]),
    .out_23(out_4[0]), .out_24(out_4[7]));
endmodule

module Greather (
  input  [7:0] in_1,
  input  [7:0] in_2,
  output out_3,
  output out_4
);

  wire [6:0] n8subtracter_1_out_4;

  _8Subtracter u_8subtracter_1 (.in_1(in_1), .in_2(in_2), .out_4({out_4, n8subtracter_1_out_4}), .out_3(out_3));
endmodule

module R_Adder (
  input  in_1,
  input  in_2,
  input  in_3,
  input  in_4,
  input  in_5,
  input  in_6,
  input  in_7,
  output [2:0] out_8
);

  wire [7:0] n8adder_1_out_4, n8adder_2_out_4, n8adder_3_out_4, n8adder_4_out_4, n8adder_5_out_4,
       n8adder_6_out_4;
  wire [7:3] n8adder_7_out_4;

  _8Adder u_8adder_1 (.in_1(8'h1), .in_2({{7{1'b0}}, in_1}), .out_4(n8adder_1_out_4));  // open: overflow
  _8Adder u_8adder_2 (.in_1(n8adder_1_out_4), .in_2({{7{1'b0}}, in_2}), .out_4(n8adder_2_out_4));  // open: overflow
  _8Adder u_8adder_3 (.in_1(n8adder_2_out_4), .in_2({{7{1'b0}}, in_3}), .out_4(n8adder_3_out_4));  // open: overflow
  _8Adder u_8adder_4 (.in_1(n8adder_3_out_4), .in_2({{7{1'b0}}, in_4}), .out_4(n8adder_4_out_4));  // open: overflow
  _8Adder u_8adder_5 (.in_1(n8adder_4_out_4), .in_2({{7{1'b0}}, in_5}), .out_4(n8adder_5_out_4));  // open: overflow
  _8Adder u_8adder_6 (.in_1(n8adder_5_out_4), .in_2({{7{1'b0}}, in_6}), .out_4(n8adder_6_out_4));  // open: overflow
  _8Adder u_8adder_7 (
    .in_1(n8adder_6_out_4), .in_2({{7{1'b0}}, in_7}), .out_4({n8adder_7_out_4, out_8}));  // open: overflow
endmodule

module R_Shifter (
  input  [7:0] in_1,
  output [7:0] out_2
);

  wire [0:0] not_1_out, not_2_out, not_3_out, not_4_out, not_5_out, not_6_out, not_7_out, not_8_out;
  wire [2:0] n8adder_7_out_4;
  wire [7:0] n8adder_1_out_4, n8adder_2_out_4, n8adder_3_out_4, n8adder_4_out_4, n8adder_5_out_4,
       n8adder_6_out_4, shifter_1_out, shifter_2_out, shifter_3_out, shifter_4_out, shifter_5_out,
       shifter_6_out, shifter_7_out;
  wire [7:3] n8adder_7_out_4_2;

  Shifter shifter_1 (.in(in_1), .\dist ({2'b00, not_1_out[0]}), .out(shifter_1_out));
  not not_1 (not_1_out[0], in_1[6]);
  _8Adder u_8adder_1 (
    .in_1({{7{1'b0}}, not_2_out[0]}), .in_2({{7{1'b0}}, not_1_out[0]}), .out_4(n8adder_1_out_4));  // open: overflow
  _8Adder u_8adder_2 (
    .in_1({{7{1'b0}}, not_3_out[0]}), .in_2(n8adder_1_out_4), .out_4(n8adder_2_out_4));  // open: overflow
  not not_2 (not_2_out[0], shifter_1_out[6]);
  _8Adder u_8adder_3 (
    .in_1({{7{1'b0}}, not_4_out[0]}), .in_2(n8adder_2_out_4), .out_4(n8adder_3_out_4));  // open: overflow
  _8Adder u_8adder_4 (
    .in_1({{7{1'b0}}, not_5_out[0]}), .in_2(n8adder_3_out_4), .out_4(n8adder_4_out_4));  // open: overflow
  _8Adder u_8adder_5 (
    .in_1({{7{1'b0}}, not_6_out[0]}), .in_2(n8adder_4_out_4), .out_4(n8adder_5_out_4));  // open: overflow
  _8Adder u_8adder_6 (
    .in_1({{7{1'b0}}, not_7_out[0]}), .in_2(n8adder_5_out_4), .out_4(n8adder_6_out_4));  // open: overflow
  Shifter shifter_2 (.in(shifter_1_out), .\dist ({2'b00, not_2_out[0]}), .out(shifter_2_out));
  not not_3 (not_3_out[0], shifter_2_out[6]);
  _8Adder u_8adder_7 (
    .in_1({{7{1'b0}}, not_8_out[0]}), .in_2(n8adder_6_out_4), .out_4({n8adder_7_out_4_2, n8adder_7_out_4}));  // open: overflow
  Shifter shifter_3 (.in(shifter_2_out), .\dist ({2'b00, not_3_out[0]}), .out(shifter_3_out));
  not not_4 (not_4_out[0], shifter_3_out[6]);
  Shifter shifter_4 (.in(shifter_3_out), .\dist ({2'b00, not_4_out[0]}), .out(shifter_4_out));
  not not_5 (not_5_out[0], shifter_4_out[6]);
  Shifter shifter_5 (.in(shifter_4_out), .\dist ({2'b00, not_5_out[0]}), .out(shifter_5_out));
  not not_6 (not_6_out[0], shifter_5_out[6]);
  Shifter shifter_6 (.in(shifter_5_out), .\dist ({2'b00, not_6_out[0]}), .out(shifter_6_out));
  not not_7 (not_7_out[0], shifter_6_out[6]);
  Shifter shifter_7 (.in(shifter_6_out), .\dist ({2'b00, not_7_out[0]}), .out(shifter_7_out));
  not not_8 (not_8_out[0], shifter_7_out[6]);
  Multiplexer #(.select(3), .width(8), .disabled(0)) multiplexer_1 (
    .in0(in_1), .in1(shifter_1_out), .in2(shifter_2_out), .in3(shifter_3_out), .in4(shifter_4_out),
    .in5(shifter_5_out), .in6(shifter_6_out), .in7(shifter_7_out), .out(out_2), .sel(n8adder_7_out_4));  // open: en
endmodule

module DivisorUnity (
  input  in_1,
  input  [7:0] original,
  input  [7:0] dividendo,
  input  [7:0] divisor,
  output parou_nesse,
  output [7:0] out_6,
  output resultado,
  output [7:0] out_8
);

  wire greather_1_out_4, not_1_out;
  wire [7:0] n8subtracter_1_out_4;

  Greather greather_1 (.in_1(divisor), .in_2(original), .out_4(greather_1_out_4));  // open: out_3
  _8Subtracter u_8subtracter_1 (.in_1(dividendo), .in_2(divisor), .out_4(n8subtracter_1_out_4));  // open: out_3
  not not_1 (not_1_out, n8subtracter_1_out_4[7]);
  Shifter #(.shift("lr")) shifter_1 (.in(divisor), .\dist (3'b001), .out(out_8));
  or or_1 (parou_nesse, in_1, greather_1_out_4);
  Multiplexer #(.width(8)) multiplexer_1 (
    .in0(dividendo), .in1(n8subtracter_1_out_4), .out(out_6), .sel(not_1_out));  // open: en
  Multiplexer multiplexer_2 (.in0(not_1_out), .in1(1'b0), .out(resultado), .sel(parou_nesse));  // open: en

  // Other names for the same wires on the sheet: se_parou_nesse = parou_nesse

  // Notes on the sheet:
  //   divisor
  //   parou no anterior?
  //   atuais
endmodule

module Divisor (
  input  [7:0] divisor,
  input  [7:0] dividendo,
  output out_3,
  output [7:0] resto,
  output [7:0] quociente
);

  wire and_1_out, and_2_out, divisorunity_1_parou_nesse, divisorunity_2_parou_nesse,
       divisorunity_3_parou_nesse, divisorunity_4_parou_nesse, divisorunity_5_parou_nesse,
       divisorunity_6_parou_nesse, divisorunity_7_parou_nesse, nor_1_out, nor_2_out, not_1_out, xor_1_out,
       xor_2_out;
  wire [2:0] r_adder_1_out_8;
  wire [7:0] complemento2_1_out_2, complemento2_2_out_2, complemento2_3_out_2, complemento2_4_out_2,
       divisorunity_1_out_6, divisorunity_1_out_8, divisorunity_2_out_6, divisorunity_2_out_8,
       divisorunity_3_out_6, divisorunity_3_out_8, divisorunity_4_out_6, divisorunity_4_out_8,
       divisorunity_5_out_6, divisorunity_5_out_8, divisorunity_6_out_6, divisorunity_6_out_8,
       divisorunity_7_out_6, divisorunity_7_out_8, divisorunity_8_resultado, multiplexer_2_out,
       multiplexer_3_out, multiplexer_4_out, r_shifter_1_out_2, shifter_1_out;

  Multiplexer #(.width(8), .disabled(0)) multiplexer_1 (
    .in0(multiplexer_2_out), .in1(complemento2_1_out_2), .out(resto), .sel(xor_1_out));  // open: en
  complemento2 complemento2_1 (.in_1(multiplexer_2_out), .out_2(complemento2_1_out_2));
  xor xor_1 (xor_1_out, dividendo[7], divisor[7]);
  Multiplexer #(.select(3), .width(8), .disabled(0)) multiplexer_2 (
    .in1(divisorunity_7_out_6), .in2(divisorunity_6_out_6), .in3(divisorunity_5_out_6),
    .in4(divisorunity_4_out_6), .in5(divisorunity_3_out_8), .in6(divisorunity_2_out_6),
    .in7(divisorunity_1_out_6), .out(multiplexer_2_out), .sel(r_adder_1_out_8));  // open: in0, en
  Multiplexer #(.width(8), .disabled(0)) multiplexer_3 (
    .in0(divisor), .in1(complemento2_2_out_2), .out(multiplexer_3_out), .sel(divisor[7]));  // open: en
  complemento2 complemento2_2 (.in_1(divisor), .out_2(complemento2_2_out_2));
  R_Shifter r_shifter_1 (.in_1(multiplexer_3_out), .out_2(r_shifter_1_out_2));
  complemento2 complemento2_3 (.in_1(dividendo), .out_2(complemento2_3_out_2));
  Multiplexer #(.width(8), .disabled(0)) multiplexer_4 (
    .in0(dividendo), .in1(complemento2_3_out_2), .out(multiplexer_4_out), .sel(dividendo[7]));  // open: en
  DivisorUnity divisorunity_1 (
    .in_1(1'b0), .parou_nesse(divisorunity_1_parou_nesse), .resultado(divisorunity_8_resultado[7]),
    .original(multiplexer_3_out), .dividendo(multiplexer_4_out), .divisor(r_shifter_1_out_2),
    .out_6(divisorunity_1_out_6), .out_8(divisorunity_1_out_8));
  DivisorUnity divisorunity_2 (
    .in_1(divisorunity_1_parou_nesse), .parou_nesse(divisorunity_2_parou_nesse),
    .resultado(divisorunity_8_resultado[6]), .original(multiplexer_3_out), .dividendo(divisorunity_1_out_6),
    .divisor(divisorunity_1_out_8), .out_6(divisorunity_2_out_6), .out_8(divisorunity_2_out_8));
  DivisorUnity divisorunity_3 (
    .in_1(divisorunity_2_parou_nesse), .parou_nesse(divisorunity_3_parou_nesse),
    .resultado(divisorunity_8_resultado[5]), .original(multiplexer_3_out), .dividendo(divisorunity_2_out_6),
    .divisor(divisorunity_2_out_8), .out_6(divisorunity_3_out_6), .out_8(divisorunity_3_out_8));
  DivisorUnity divisorunity_4 (
    .in_1(divisorunity_3_parou_nesse), .parou_nesse(divisorunity_4_parou_nesse),
    .resultado(divisorunity_8_resultado[4]), .original(multiplexer_3_out), .dividendo(divisorunity_3_out_6),
    .divisor(divisorunity_3_out_8), .out_6(divisorunity_4_out_6), .out_8(divisorunity_4_out_8));
  DivisorUnity divisorunity_5 (
    .in_1(divisorunity_4_parou_nesse), .parou_nesse(divisorunity_5_parou_nesse),
    .resultado(divisorunity_8_resultado[3]), .original(multiplexer_3_out), .dividendo(divisorunity_4_out_6),
    .divisor(divisorunity_4_out_8), .out_6(divisorunity_5_out_6), .out_8(divisorunity_5_out_8));
  DivisorUnity divisorunity_6 (
    .in_1(divisorunity_5_parou_nesse), .parou_nesse(divisorunity_6_parou_nesse),
    .resultado(divisorunity_8_resultado[2]), .original(multiplexer_3_out), .dividendo(divisorunity_5_out_6),
    .divisor(divisorunity_5_out_8), .out_6(divisorunity_6_out_6), .out_8(divisorunity_6_out_8));
  DivisorUnity divisorunity_7 (
    .in_1(divisorunity_6_parou_nesse), .parou_nesse(divisorunity_7_parou_nesse),
    .resultado(divisorunity_8_resultado[1]), .original(multiplexer_3_out), .dividendo(divisorunity_6_out_6),
    .divisor(divisorunity_6_out_8), .out_6(divisorunity_7_out_6), .out_8(divisorunity_7_out_8));
  DivisorUnity divisorunity_8 (
    .in_1(divisorunity_7_parou_nesse), .resultado(divisorunity_8_resultado[0]), .original(multiplexer_3_out),
    .dividendo(divisorunity_7_out_6), .divisor(divisorunity_7_out_8));  // open: parou_nesse, out_6, out_8
  R_Adder r_adder_1 (
    .in_1(divisorunity_1_parou_nesse), .in_2(divisorunity_2_parou_nesse), .in_3(divisorunity_3_parou_nesse),
    .in_4(divisorunity_4_parou_nesse), .in_5(divisorunity_5_parou_nesse), .in_6(divisorunity_6_parou_nesse),
    .in_7(divisorunity_7_parou_nesse), .out_8(r_adder_1_out_8));
  Shifter #(.shift("lr")) shifter_1 (.in(divisorunity_8_resultado), .\dist (r_adder_1_out_8), .out(shifter_1_out));
  nor nor_1 (nor_1_out, divisor[0], divisor[1], divisor[2], divisor[3], divisor[4], divisor[5], divisor[6], divisor[7]);
  nor nor_2 (nor_2_out, dividendo[0], dividendo[1], dividendo[2], dividendo[3], dividendo[4], dividendo[5], dividendo[6]);
  and and_1 (and_1_out, divisor[0], divisor[1], divisor[2], divisor[3], divisor[4], divisor[5], divisor[6], divisor[7]);
  xor xor_2 (xor_2_out, dividendo[7], divisor[7]);
  complemento2 complemento2_4 (.in_1(shifter_1_out), .out_2(complemento2_4_out_2));
  and and_2 (and_2_out, nor_2_out, dividendo[7], and_1_out);
  not not_1 (not_1_out, xor_2_out);
  Multiplexer #(.width(8), .disabled(0)) multiplexer_5 (
    .in0(complemento2_4_out_2), .in1(shifter_1_out), .out(quociente), .sel(not_1_out));  // open: en
  or or_1 (out_3, and_2_out, nor_1_out);

  // Other names for the same wires on the sheet: overflow[7:0] = divisor; signal1 = divisor[7];
  //   overflow_0[7:0] = dividendo; signal0 = dividendo[7]
endmodule

module ALU (
  input  in_1,
  input  in_2,
  input  in_3,
  input  in_4,
  input  A,
  input  in_6,
  input  in_7,
  input  in_8,
  input  in_9,
  input  in_10,
  input  in_11,
  input  B,
  input  in_13,
  input  in_14,
  input  in_15,
  input  in_16,
  input  in_17,
  input  Op,
  input  in_19,
  output Overflow,
  output out_21,
  output out_22,
  output out_23,
  output out_24,
  output out_25,
  output out_26,
  output out_27,
  output out_28
);

  wire divisor_1_out_3, n8adder_1_overflow, n8multiplier_1_out_3, n8subtracter_1_out_3;
  wire [7:0] divisor_1_quociente, divisor_1_resto, n8adder_1_out_4, n8multiplier_1_out_4,
       n8subtracter_1_out_4;
  wire [15:0] demultiplexer_1_out0, demultiplexer_1_out1, demultiplexer_1_out2, demultiplexer_1_out3,
       demultiplexer_1_out4, multiplexer_1_out;

  Demultiplexer #(.select(3), .width(16), .disabled(0)) demultiplexer_1 (
    .out0(demultiplexer_1_out0), .out1(demultiplexer_1_out1), .out2(demultiplexer_1_out2),
    .out3(demultiplexer_1_out3), .out4(demultiplexer_1_out4),
    .in({in_16, in_15, in_14, in_13, B, in_11, in_10, in_9, in_8, in_7, in_6, A, in_4, in_3, in_2, in_1}),
    .sel({in_19, Op, in_17}));  // open: out5, out6, out7, en
  Multiplexer #(.width(16)) multiplexer_1 (
    .in0(demultiplexer_1_out3), .in1(demultiplexer_1_out4), .out(multiplexer_1_out), .en(in_19));  // open: sel
  Multiplexer #(.select(3), .disabled(0)) multiplexer_2 (
    .in0(n8adder_1_overflow), .in1(n8subtracter_1_out_3), .in2(n8multiplier_1_out_3), .in3(divisor_1_out_3),
    .out(Overflow), .sel({in_19, Op, in_17}));  // open: in4, in5, in6, in7, en
  _8Adder u_8adder_1 (
    .in_1(demultiplexer_1_out0[7:0]), .in_2(demultiplexer_1_out0[15:8]), .out_4(n8adder_1_out_4),
    .overflow(n8adder_1_overflow));
  _8Subtracter u_8subtracter_1 (
    .in_1(demultiplexer_1_out1[7:0]), .in_2(demultiplexer_1_out1[15:8]), .out_4(n8subtracter_1_out_4),
    .out_3(n8subtracter_1_out_3));
  _8Multiplier u_8multiplier_1 (
    .in_1(demultiplexer_1_out2[7:0]), .in_2(demultiplexer_1_out2[15:8]), .out_4(n8multiplier_1_out_4),
    .out_3(n8multiplier_1_out_3));
  Divisor divisor_1 (
    .resto(divisor_1_resto), .out_3(divisor_1_out_3), .quociente(divisor_1_quociente),
    .divisor(multiplexer_1_out[15:8]), .dividendo(multiplexer_1_out[7:0]));
  Multiplexer #(.select(3), .width(8), .disabled(0)) multiplexer_3 (
    .in0(n8adder_1_out_4), .in1(n8subtracter_1_out_4), .in2(n8multiplier_1_out_4), .in3(divisor_1_quociente),
    .in4(divisor_1_resto), .out({out_28, out_27, out_26, out_25, out_24, out_23, out_22, out_21}),
    .sel({in_19, Op, in_17}));  // open: in5, in6, in7, en

  // Other names for the same wires on the sheet: choice[2:0] = {in_19, Op, in_17}

  // Notes on the sheet:
  //   Resultado
endmodule

module Equal (
  input  [7:0] in_1,
  input  [7:0] in_2,
  output out_3
);

  wire xnor_1_out, xnor_2_out, xnor_3_out, xnor_4_out, xnor_5_out, xnor_6_out, xnor_7_out, xnor_8_out;

  xnor xnor_1 (xnor_1_out, in_2[0], in_1[0]);
  xnor xnor_2 (xnor_2_out, in_1[1], in_2[1]);
  xnor xnor_3 (xnor_3_out, in_1[2], in_2[2]);
  xnor xnor_4 (xnor_4_out, in_1[3], in_2[3]);
  xnor xnor_5 (xnor_5_out, in_1[4], in_2[4]);
  xnor xnor_6 (xnor_6_out, in_1[5], in_2[5]);
  xnor xnor_7 (xnor_7_out, in_1[6], in_2[6]);
  xnor xnor_8 (xnor_8_out, in_1[7], in_2[7]);
  and and_1 (out_3, xnor_1_out, xnor_2_out, xnor_3_out, xnor_4_out, xnor_5_out, xnor_6_out, xnor_7_out, xnor_8_out);

  // Other names for the same wires on the sheet: _0 = in_2[0]; _1 = in_2[1]; _2 = in_2[2]; _3 = in_2[3]; _4 = in_2[4];
  //   _5 = in_2[5]; _6 = in_2[6]; _7 = in_2[7]
endmodule

module PC (
  input  clear,
  input  clock,
  input  set,
  input  [7:0] SET_2,
  output [7:0] out_5
);

  wire and_1_out, and_2_out, and_3_out, and_4_out, and_5_out, and_6_out, and_7_out, controlled_buffer_1_out,
       controlled_buffer_4_out, controlled_buffer_6_out, controlled_buffer_7_out, controlled_buffer_9_out,
       controlled_buffer_11_out, controlled_buffer_13_out, controlled_buffer_15_out,
       controlled_buffer_17_out, not_1_out, not_2_out, not_3_out, not_4_out, not_5_out, not_6_out, not_7_out,
       not_8_out, not_9_out, not_10_out, not_11_out, not_12_out, not_13_out, not_14_out, not_15_out,
       not_16_out, not_17_out, not_18_out, not_19_out, not_20_out, not_21_out, not_22_out, not_23_out,
       not_24_out, not_25_out, pull_resistor_1_node, pull_resistor_2_node, pull_resistor_3_node,
       pull_resistor_4_node, pull_resistor_5_node, pull_resistor_6_node, pull_resistor_7_node,
       pull_resistor_8_node;

  and and_1 (and_1_out, out_5[0], out_5[1], out_5[2], out_5[3], out_5[4], out_5[5], out_5[6]);
  assign controlled_buffer_1_out = not_3_out ? controlled_buffer_17_out : 1'bz;  // Controlled_Buffer controlled_buffer_1
  not not_1 (not_1_out, not_2_out);
  not not_2 (not_2_out, pull_resistor_1_node);
  not not_3 (not_3_out, and_7_out);
  Pull_Resistor pull_resistor_1 (.node(pull_resistor_1_node));
  assign pull_resistor_1_node = and_7_out ? SET_2[7] : 1'bz;  // Controlled_Buffer controlled_buffer_2
  and and_2 (and_2_out, out_5[0], out_5[1], out_5[2], out_5[3], out_5[4], out_5[5]);
  J_K_Flip_Flop j_k_ff_1 (
    .J(and_1_out), .clk(clock), .K(and_1_out), .Q(out_5[7]), .preset(not_1_out), .en(1'b1),
    .reset(controlled_buffer_1_out));  // open: Qn
  not not_4 (not_4_out, not_5_out);
  not not_5 (not_5_out, pull_resistor_2_node);
  Pull_Resistor pull_resistor_2 (.node(pull_resistor_2_node));
  assign controlled_buffer_1_out = and_7_out ? ~SET_2[7] : 1'bz;  // Controlled_Inverter controlled_inverter_1
  assign pull_resistor_2_node = and_7_out ? SET_2[6] : 1'bz;  // Controlled_Buffer controlled_buffer_3
  and and_3 (and_3_out, out_5[0], out_5[1], out_5[2], out_5[3], out_5[4]);
  J_K_Flip_Flop j_k_ff_2 (
    .J(and_2_out), .clk(clock), .K(and_2_out), .Q(out_5[6]), .preset(not_4_out), .en(1'b1),
    .reset(controlled_buffer_4_out));  // open: Qn
  assign controlled_buffer_4_out = not_8_out ? controlled_buffer_17_out : 1'bz;  // Controlled_Buffer controlled_buffer_4
  not not_6 (not_6_out, not_7_out);
  not not_7 (not_7_out, pull_resistor_3_node);
  not not_8 (not_8_out, and_7_out);
  assign controlled_buffer_4_out = and_7_out ? ~SET_2[6] : 1'bz;  // Controlled_Inverter controlled_inverter_2
  Pull_Resistor pull_resistor_3 (.node(pull_resistor_3_node));
  assign pull_resistor_3_node = and_7_out ? SET_2[5] : 1'bz;  // Controlled_Buffer controlled_buffer_5
  J_K_Flip_Flop j_k_ff_3 (
    .J(and_3_out), .clk(clock), .K(and_3_out), .Q(out_5[5]), .preset(not_6_out), .en(1'b1),
    .reset(controlled_buffer_6_out));  // open: Qn
  assign controlled_buffer_6_out = not_9_out ? controlled_buffer_17_out : 1'bz;  // Controlled_Buffer controlled_buffer_6
  not not_9 (not_9_out, and_7_out);
  assign controlled_buffer_6_out = and_7_out ? ~SET_2[5] : 1'bz;  // Controlled_Inverter controlled_inverter_3
  and and_4 (and_4_out, out_5[0], out_5[1], out_5[2], out_5[3]);
  J_K_Flip_Flop j_k_ff_4 (
    .J(and_4_out), .clk(clock), .K(and_4_out), .Q(out_5[4]), .preset(not_10_out), .en(1'b1),
    .reset(controlled_buffer_7_out));  // open: Qn
  assign controlled_buffer_7_out = not_12_out ? controlled_buffer_17_out : 1'bz;  // Controlled_Buffer controlled_buffer_7
  not not_10 (not_10_out, not_11_out);
  not not_11 (not_11_out, pull_resistor_4_node);
  not not_12 (not_12_out, and_7_out);
  Pull_Resistor pull_resistor_4 (.node(pull_resistor_4_node));
  assign controlled_buffer_7_out = and_7_out ? ~SET_2[4] : 1'bz;  // Controlled_Inverter controlled_inverter_4
  assign pull_resistor_4_node = and_7_out ? SET_2[4] : 1'bz;  // Controlled_Buffer controlled_buffer_8
  and and_5 (and_5_out, out_5[0], out_5[1], out_5[2]);
  J_K_Flip_Flop j_k_ff_5 (
    .J(and_5_out), .clk(clock), .K(and_5_out), .Q(out_5[3]), .preset(not_13_out), .en(1'b1),
    .reset(controlled_buffer_9_out));  // open: Qn
  assign controlled_buffer_9_out = not_15_out ? controlled_buffer_17_out : 1'bz;  // Controlled_Buffer controlled_buffer_9
  not not_13 (not_13_out, not_14_out);
  not not_14 (not_14_out, pull_resistor_5_node);
  not not_15 (not_15_out, and_7_out);
  Pull_Resistor pull_resistor_5 (.node(pull_resistor_5_node));
  assign controlled_buffer_9_out = and_7_out ? ~SET_2[3] : 1'bz;  // Controlled_Inverter controlled_inverter_5
  assign pull_resistor_5_node = and_7_out ? SET_2[3] : 1'bz;  // Controlled_Buffer controlled_buffer_10
  J_K_Flip_Flop j_k_ff_6 (
    .J(and_6_out), .clk(clock), .K(and_6_out), .Q(out_5[2]), .preset(not_16_out), .en(1'b1),
    .reset(controlled_buffer_11_out));  // open: Qn
  assign controlled_buffer_11_out = not_18_out ? controlled_buffer_17_out : 1'bz;  // Controlled_Buffer controlled_buffer_11
  not not_16 (not_16_out, not_17_out);
  not not_17 (not_17_out, pull_resistor_6_node);
  not not_18 (not_18_out, and_7_out);
  assign controlled_buffer_11_out = and_7_out ? ~SET_2[2] : 1'bz;  // Controlled_Inverter controlled_inverter_6
  Pull_Resistor pull_resistor_6 (.node(pull_resistor_6_node));
  assign pull_resistor_6_node = and_7_out ? SET_2[2] : 1'bz;  // Controlled_Buffer controlled_buffer_12
  and and_6 (and_6_out, out_5[0], out_5[1]);
  J_K_Flip_Flop j_k_ff_7 (
    .J(out_5[0]), .clk(clock), .K(out_5[0]), .Q(out_5[1]), .preset(not_19_out), .en(1'b1),
    .reset(controlled_buffer_13_out));  // open: Qn
  assign controlled_buffer_13_out = not_21_out ? controlled_buffer_17_out : 1'bz;  // Controlled_Buffer controlled_buffer_13
  not not_19 (not_19_out, not_20_out);
  not not_20 (not_20_out, pull_resistor_7_node);
  not not_21 (not_21_out, and_7_out);
  Pull_Resistor pull_resistor_7 (.node(pull_resistor_7_node));
  assign controlled_buffer_13_out = and_7_out ? ~SET_2[1] : 1'bz;  // Controlled_Inverter controlled_inverter_7
  assign pull_resistor_7_node = and_7_out ? SET_2[1] : 1'bz;  // Controlled_Buffer controlled_buffer_14
  assign controlled_buffer_15_out = not_24_out ? controlled_buffer_17_out : 1'bz;  // Controlled_Buffer controlled_buffer_15
  not not_22 (not_22_out, not_23_out);
  not not_23 (not_23_out, pull_resistor_8_node);
  not not_24 (not_24_out, and_7_out);
  Pull_Resistor pull_resistor_8 (.node(pull_resistor_8_node));
  assign pull_resistor_8_node = and_7_out ? SET_2[0] : 1'bz;  // Controlled_Buffer controlled_buffer_16
  J_K_Flip_Flop j_k_ff_8 (
    .J(1'b1), .clk(clock), .K(1'b1), .Q(out_5[0]), .preset(not_22_out), .en(1'b1),
    .reset(controlled_buffer_15_out));  // open: Qn
  assign controlled_buffer_17_out = not_24_out ? clear : 1'bz;  // Controlled_Buffer controlled_buffer_17
  assign controlled_buffer_15_out = and_7_out ? ~SET_2[0] : 1'bz;  // Controlled_Inverter controlled_inverter_8
  not not_25 (not_25_out, clock);
  and and_7 (and_7_out, not_25_out, set);
endmodule

module Ctrl (
  input  [15:0] in_1,
  input  [15:0] in_2,
  input  clock,
  output [7:0] out_4,
  output out_5,
  output out_6,
  output out_7,
  output out_8,
  output out_9,
  output out_10,
  output out_11
);

  wire and_1_out, and_2_out, and_3_out, and_4_out, and_5_out, and_6_out, G_L, JDZ, JDZ_out, JEQ, JEQ_out,
       JGE, JGE_out, JGT, JGT_out, JLE, JLT_out, JMP_out, LDA_out, not_1_out, not_2_out, not_3_out, STA_out,
       STP_out;
  wire [6:0] controlled_buffer_1_out;
  wire [7:0] A, B;

  and LDA (LDA_out, in_1[8], in_1[9], ~in_1[10], in_1[11], ~in_1[12], ~in_1[13], ~in_1[14], ~in_1[15]);  // AND_Gate
  and STA (STA_out, ~in_1[8], ~in_1[9], in_1[10], in_1[11], ~in_1[12], ~in_1[13], ~in_1[14], ~in_1[15]);  // AND_Gate
  and JMP (JMP_out, in_1[8], in_1[9], ~in_1[10], ~in_1[11], in_1[12], in_1[13], ~in_1[14], ~in_1[15]);  // AND_Gate
  and STP (STP_out, ~in_1[8], in_1[9], in_1[10], ~in_1[11], ~in_1[12], ~in_1[13], in_1[14], ~in_1[15]);  // AND_Gate
  and u_JLE (G_L, ~in_1[8], ~in_1[9], in_1[10], ~in_1[11], in_1[12], in_1[13], ~in_1[14], ~in_1[15]);  // AND_Gate
  and u_JDZ (JDZ_out, in_1[8], ~in_1[9], in_1[10], ~in_1[11], in_1[12], in_1[13], ~in_1[14], ~in_1[15]);  // AND_Gate
  and u_JGT (JGT_out, ~in_1[8], in_1[9], in_1[10], ~in_1[11], in_1[12], in_1[13], ~in_1[14], ~in_1[15]);  // AND_Gate
  and u_JEQ (JEQ_out, in_1[8], in_1[9], in_1[10], ~in_1[11], in_1[12], in_1[13], ~in_1[14], ~in_1[15]);  // AND_Gate
  and JLT (JLT_out, ~in_1[8], ~in_1[9], ~in_1[10], in_1[11], in_1[12], in_1[13], ~in_1[14], ~in_1[15]);  // AND_Gate
  and u_JGE (JGE_out, in_1[8], ~in_1[9], ~in_1[10], in_1[11], in_1[12], in_1[13], ~in_1[14], ~in_1[15]);  // AND_Gate
  and and_1 (and_1_out, JGE_out, JGE);
  assign controlled_buffer_1_out = and_1_out ? 7'b0101010 : 7'bz;  // Controlled_Buffer controlled_buffer_1
  and and_2 (and_2_out, JLT_out, JLE);
  assign controlled_buffer_1_out = and_2_out ? 7'b0101010 : 7'bz;  // Controlled_Buffer controlled_buffer_2
  and and_3 (and_3_out, JGT_out, JGT);
  assign controlled_buffer_1_out = and_3_out ? 7'b0101010 : 7'bz;  // Controlled_Buffer controlled_buffer_3
  and and_4 (and_4_out, JEQ_out, JEQ);
  assign controlled_buffer_1_out = and_4_out ? 7'b0101010 : 7'bz;  // Controlled_Buffer controlled_buffer_4
  and and_5 (and_5_out, G_L, JLE);
  and and_6 (and_6_out, JDZ_out, JDZ);
  assign controlled_buffer_1_out = and_6_out ? 7'b0101010 : 7'bz;  // Controlled_Buffer controlled_buffer_5
  assign controlled_buffer_1_out = STP_out ? 7'b0101001 : 7'bz;  // Controlled_Buffer controlled_buffer_6
  assign controlled_buffer_1_out = and_5_out ? 7'b0101010 : 7'bz;  // Controlled_Buffer controlled_buffer_7
  assign controlled_buffer_1_out = STA_out ? 7'b1000100 : 7'bz;  // Controlled_Buffer controlled_buffer_8
  assign controlled_buffer_1_out = JMP_out ? 7'b0101010 : 7'bz;  // Controlled_Buffer controlled_buffer_9
  assign out_5 = not_1_out ? controlled_buffer_1_out[6] : 1'bz;  // Controlled_Buffer controlled_buffer_10
  Pull_Resistor pull_resistor_1 (.node(out_5));
  not not_1 (not_1_out, clock);
  assign controlled_buffer_1_out = LDA_out ? 7'b1110000 : 7'bz;  // Controlled_Buffer controlled_buffer_11
  assign out_6 = not_1_out ? controlled_buffer_1_out[5] : 1'bz;  // Controlled_Buffer controlled_buffer_12
  Pull_Resistor #(.pull(1)) pull_resistor_2 (.node(out_6));
  assign out_7 = not_1_out ? controlled_buffer_1_out[4] : 1'bz;  // Controlled_Buffer controlled_buffer_13
  Pull_Resistor pull_resistor_3 (.node(out_7));
  Greather greather_1 (.in_1(B), .in_2(A), .out_4(JLE));  // open: out_3
  assign out_9 = not_1_out ? controlled_buffer_1_out[2] : 1'bz;  // Controlled_Buffer controlled_buffer_14
  assign out_8 = not_1_out ? controlled_buffer_1_out[3] : 1'bz;  // Controlled_Buffer controlled_buffer_15
  Pull_Resistor pull_resistor_4 (.node(out_9));
  Pull_Resistor #(.pull(1)) pull_resistor_5 (.node(out_8));
  assign B = G_L ? {8{1'b0}} : 8'bz;  // Controlled_Buffer controlled_buffer_16
  not not_2 (not_2_out, G_L);
  assign A = not_2_out ? {8{1'b0}} : 8'bz;  // Controlled_Buffer controlled_buffer_17
  Equal equal_1 (.in_1(A), .in_2(B), .out_3(JEQ));
  assign out_10 = not_1_out ? controlled_buffer_1_out[1] : 1'bz;  // Controlled_Buffer controlled_buffer_18
  Pull_Resistor pull_resistor_6 (.node(out_10));
  assign B = not_3_out ? in_2[7:0] : 8'bz;  // Controlled_Buffer controlled_buffer_19
  not not_3 (not_3_out, G_L);
  assign A = G_L ? in_2[7:0] : 8'bz;  // Controlled_Buffer controlled_buffer_20
  not not_4 (JGT, JLE);
  not not_5 (JGE, JLE);
  not not_6 (JDZ, JEQ);
  assign out_11 = not_1_out ? controlled_buffer_1_out[0] : 1'bz;  // Controlled_Buffer controlled_buffer_21
  Pull_Resistor pull_resistor_7 (.node(out_11));

  assign out_4 = in_1[7:0];

  // Other names for the same wires on the sheet: JLT = JLE

  // Notes on the sheet:
  //   clock: pull=down
  //   Que significam:
  //   instrução
  //   São 7 bits que irão controlar, respectivamente:
  //   W_ctrl, RW, R_acc, R_ir, write_acc, set_pc, clear
  //   Essas constantes representam a execução da instrução.
  //   RW: Se a RAM estará em modo Read ou Write ( 1 para Read )
  //   endereço
  //   W_ctrl: Se quem vai dizer o proximo endereço para a RAM é o PC ou o Ctrl direto
  //   set_pc: informa o circuito do PC se ele deve ter seu valor mudado pelo controle ou não
  //   clear: informa o flip-flop que cuida do desligamento da CPU se ele deve desliga-lá ou não
  //   R_acc: controla o buffer que manda o conteudo da RAM para ACC ( ativado quando ACC deve receber um valor )
  //   R_ir: controla o buffer que manda o countedo da RAM para IR ( ativado quando IR deve receber uma instrução )
  //   write_acc: controla o buffer que manda o conteúdo de ACC para RAM ( ativado se o conteúdo de ACC deve ser escrito na RAM )
  //   01101001
  //   10000100
  //   01101010
  //   11000000
  //   ACC
  //   Execução
  //   default:NOP
endmodule

module CPU (
  output [15:0] out_1,
  output [15:0] out_2,
  output [15:0] out_3,
  output [7:0] out_4
);

  wire and_1_out, \begin , button_1_out, clear, clock_1_out, clock_2_out, clock_3_out, clock_4_out,
       clock_5_out, clock_6_out, ctrl_1_out_5, ctrl_1_out_6, ctrl_1_out_7, ctrl_1_out_8, ctrl_1_out_9,
       ctrl_1_out_10, ctrl_1_out_11, j_k_ff_2_qn, ligado, not_1_out, not_2_out, not_3_out, not_4_out,
       not_5_out;
  wire [7:0] ctrl_1_out_4, pc_1_out_5;
  wire [15:0] controlled_buffer_3_out, controlled_buffer_4_out, register_1_q;

  assign out_4 = not_1_out ? pc_1_out_5 : 8'bz;  // Controlled_Buffer controlled_buffer_1
  not not_1 (not_1_out, ctrl_1_out_5);
  PC pc_1 (.clear(clear), .clock(and_1_out), .set(ctrl_1_out_10), .SET_2(ctrl_1_out_4), .out_5(pc_1_out_5));
  not not_2 (not_2_out, clock_1_out);
  Clock clock_1 (.out(clock_1_out));
  and and_1 (and_1_out, not_2_out, \begin );
  assign out_4 = ctrl_1_out_5 ? ctrl_1_out_4 : 8'bz;  // Controlled_Buffer controlled_buffer_2
  not not_3 (not_3_out, clock_2_out);
  Clock clock_2 (.out(clock_2_out));
  RAM #(.dataWidth(16)) ram_1 (
    .addr(out_4), .data(out_1), .sel(ligado), .clk(not_4_out), .ld(ctrl_1_out_6));  // open: clr
  not not_4 (not_4_out, clock_3_out);
  Clock clock_3 (.out(clock_3_out));
  assign controlled_buffer_3_out = ctrl_1_out_7 ? out_1 : 16'bz;  // Controlled_Buffer controlled_buffer_3
  Clock clock_4 (.out(clock_4_out));
  Ctrl ctrl_1 (
    .in_1(out_2), .out_4(ctrl_1_out_4), .out_5(ctrl_1_out_5), .out_6(ctrl_1_out_6), .out_7(ctrl_1_out_7),
    .out_8(ctrl_1_out_8), .out_9(ctrl_1_out_9), .out_10(ctrl_1_out_10), .out_11(ctrl_1_out_11),
    .clock(not_3_out), .in_2(out_1));
  assign controlled_buffer_4_out = ctrl_1_out_8 ? out_1 : 16'bz;  // Controlled_Buffer controlled_buffer_4
  Register #(.width(16), .trigger("high")) register_1 (
    .D(controlled_buffer_3_out), .en(ligado), .Q(register_1_q), .clk(clock_4_out), .clr(clear));
  assign out_1 = ctrl_1_out_9 ? register_1_q : 16'bz;  // Controlled_Buffer controlled_buffer_5
  Register #(.width(16), .trigger("high")) register_2 (
    .D(controlled_buffer_4_out), .en(ligado), .Q(out_2), .clk(not_5_out), .clr(clear));
  not not_5 (not_5_out, clock_5_out);
  Clock clock_5 (.out(clock_5_out));
  Clock clock_6 (.out(clock_6_out));
  Button button_1 (.out(button_1_out));
  J_K_Flip_Flop j_k_ff_1 (
    .J(1'b1), .clk(clock_6_out), .K(1'b0), .Q(\begin ), .en(ligado), .reset(clear));  // open: Qn, preset
  J_K_Flip_Flop j_k_ff_2 (
    .J(1'b1), .clk(button_1_out), .K(1'b1), .Q(ligado), .Qn(j_k_ff_2_qn), .en(1'b1), .reset(ctrl_1_out_11));  // open: preset
  or or_1 (clear, j_k_ff_2_qn, ctrl_1_out_11);

  assign out_3 = out_1;

  // Other names for the same wires on the sheet: A[7:0] = out_4; ACC[15:0] = out_1; D[15:0] = out_1; IR[15:0] = out_2

  // Notes on the sheet:
  //   Para ligar a CPU, pressionar o botao START
  //   R_ir
  //   ACC
  //   IR
  //   START
  //   Valores:
  //   a instrucao STP desliga a CPU
  //   Como o PC se auto-incrementa quando recebe o clock,
  //   esse flip-flop impede que ele faça isso no primeiro pulso.
endmodule
