// Logisim project divider8.circ as structural Verilog: 7 circuits, main circuit full subtractor
module full_divider (
  input  [7:0] divisor,
  input  [7:0] quociente,
  output [7:0] quociente_final,
  output [7:0] resto_final
);

  wire [7:0] divider_unity_1_novo_quociente, divider_unity_1_novo_resto, divider_unity_2_novo_quociente,
       divider_unity_2_novo_resto, divider_unity_3_novo_quociente, divider_unity_3_novo_resto,
       divider_unity_4_novo_quociente, divider_unity_4_novo_resto, divider_unity_5_novo_quociente,
       divider_unity_5_novo_resto, divider_unity_6_novo_quociente, divider_unity_6_novo_resto,
       divider_unity_7_novo_quociente, divider_unity_7_novo_resto;

  divider_unity divider_unity_1 (
    .Divisor(divisor), .Resto({8{1'b0}}), .Quociente(quociente),
    .novo_quociente(divider_unity_1_novo_quociente), .novo_resto(divider_unity_1_novo_resto));
  divider_unity divider_unity_2 (
    .Divisor(divisor), .Resto(divider_unity_1_novo_resto), .Quociente(divider_unity_1_novo_quociente),
    .novo_quociente(divider_unity_2_novo_quociente), .novo_resto(divider_unity_2_novo_resto));
  divider_unity divider_unity_3 (
    .Divisor(divisor), .Resto(divider_unity_2_novo_resto), .Quociente(divider_unity_2_novo_quociente),
    .novo_quociente(divider_unity_3_novo_quociente), .novo_resto(divider_unity_3_novo_resto));
  divider_unity divider_unity_4 (
    .Divisor(divisor), .Resto(divider_unity_3_novo_resto), .Quociente(divider_unity_3_novo_quociente),
    .novo_quociente(divider_unity_4_novo_quociente), .novo_resto(divider_unity_4_novo_resto));
  divider_unity divider_unity_5 (
    .Divisor(divisor), .Resto(divider_unity_4_novo_resto), .Quociente(divider_unity_4_novo_quociente),
    .novo_quociente(divider_unity_5_novo_quociente), .novo_resto(divider_unity_5_novo_resto));
  divider_unity divider_unity_6 (
    .Divisor(divisor), .Resto(divider_unity_5_novo_resto), .Quociente(divider_unity_5_novo_quociente),
    .novo_quociente(divider_unity_6_novo_quociente), .novo_resto(divider_unity_6_novo_resto));
  divider_unity divider_unity_7 (
    .Divisor(divisor), .Resto(divider_unity_6_novo_resto), .Quociente(divider_unity_6_novo_quociente),
    .novo_quociente(divider_unity_7_novo_quociente), .novo_resto(divider_unity_7_novo_resto));
  divider_unity divider_unity_8 (
    .Divisor(divisor), .Resto(divider_unity_7_novo_resto), .Quociente(divider_unity_7_novo_quociente),
    .novo_quociente(quociente_final), .novo_resto(resto_final));
endmodule

module divider_unity (
  input  [7:0] Resto,
  input  [7:0] Quociente,
  input  [7:0] Divisor,
  output [7:0] novo_quociente,
  output [7:0] novo_resto
);

  wire full_subtractor_1_sign;
  wire [7:0] full_subtractor_1_sub, set_rightmost_1_out_16, shifter_1_out_24, shifter_1_out_32;

  full_subtractor full_subtractor_1 (
    .A(shifter_1_out_24), .B(Divisor), .in_1(1'b0), .Sub(full_subtractor_1_sub), .sign(full_subtractor_1_sign));
  Multiplexer #(.width(8)) multiplexer_1 (
    .in0(full_subtractor_1_sub), .in1(shifter_1_out_24), .out(novo_resto), .sel(full_subtractor_1_sign));  // open: en
  shifter shifter_1 (
    .in_1(Resto[7]), .in_2(Resto[6]), .in_3(Resto[5]), .in_4(Resto[4]), .in_5(Resto[3]), .in_6(Resto[2]),
    .in_7(Resto[1]), .in_8(Resto[0]), .in_9(Quociente[7]), .in_10(Quociente[6]), .in_11(Quociente[5]),
    .QUOCIENTE(Quociente[4]), .in_13(Quociente[3]), .in_14(Quociente[2]), .in_15(Quociente[1]),
    .in_16(Quociente[0]), .out_17(shifter_1_out_24[7]), .out_18(shifter_1_out_24[6]),
    .out_19(shifter_1_out_24[5]), .out_20(shifter_1_out_24[4]), .out_21(shifter_1_out_24[3]),
    .out_22(shifter_1_out_24[2]), .out_23(shifter_1_out_24[1]), .out_24(shifter_1_out_24[0]),
    .out_25(shifter_1_out_32[7]), .out_26(shifter_1_out_32[6]), .out_27(shifter_1_out_32[5]),
    .out_28(shifter_1_out_32[4]), .out_29(shifter_1_out_32[3]), .out_30(shifter_1_out_32[2]),
    .out_31(shifter_1_out_32[1]), .out_32(shifter_1_out_32[0]));
  set_rightmost set_rightmost_1 (
    .q7(shifter_1_out_32[7]), .in_2(shifter_1_out_32[6]), .in_3(shifter_1_out_32[5]),
    .quociente(shifter_1_out_32[4]), .in_5(shifter_1_out_32[3]), .in_6(shifter_1_out_32[2]),
    .in_7(shifter_1_out_32[1]), .in_8(shifter_1_out_32[0]), .out_9(set_rightmost_1_out_16[7]),
    .out_10(set_rightmost_1_out_16[6]), .out_11(set_rightmost_1_out_16[5]),
    .out_12(set_rightmost_1_out_16[4]), .out_13(set_rightmost_1_out_16[3]),
    .out_14(set_rightmost_1_out_16[2]), .out_15(set_rightmost_1_out_16[1]), .out_16(set_rightmost_1_out_16[0]));
  Multiplexer #(.width(8)) multiplexer_2 (
    .in0(set_rightmost_1_out_16), .in1(shifter_1_out_32), .out(novo_quociente), .sel(full_subtractor_1_sign));  // open: en

  // Notes on the sheet:
  //   subtracao
endmodule

module full_subtractor (
  input  in_1,
  input  [7:0] A,
  input  [7:0] B,
  output [7:0] Sub,
  output sign
);

  _8bitSub u_8bitsub_1 (
    .out_18(Sub[0]), .out_19(Sub[1]), .out_20(Sub[2]), .out_21(Sub[3]), .out_22(Sub[4]), .out_23(Sub[5]),
    .out_24(Sub[6]), .out_25(Sub[7]), .a6(A[6]), .a7(A[7]), .c0(in_1), .a0(A[0]), .a1(A[1]), .a2(A[2]),
    .a3(A[3]), .a4(A[4]), .a5(A[5]), .b0(B[0]), .b1(B[1]), .b2(B[2]), .b3(B[3]), .b4(B[4]), .b5(B[5]),
    .b6(B[6]), .b7(B[7]), .sign(sign));
endmodule

module subtract (
  input  Ai,
  input  Bi,
  input  CI,
  output SUM,
  output CI_1
);

  wire and_1_out, and_2_out, not_1_out, xor_1_out;

  not not_1 (not_1_out, Bi);
  xor xor_1 (xor_1_out, Ai, not_1_out);
  and and_1 (and_1_out, Ai, not_1_out);
  and and_2 (and_2_out, xor_1_out, CI);
  or or_1 (CI_1, and_1_out, and_2_out);
  xor xor_2 (SUM, xor_1_out, CI);

  // Notes on the sheet:
  //   BI
endmodule

module shifter (
  input  in_1,
  input  in_2,
  input  in_3,
  input  in_4,
  input  in_5,
  input  in_6,
  input  in_7,
  input  in_8,
  input  in_9,
  input  in_10,
  input  in_11,
  input  QUOCIENTE,
  input  in_13,
  input  in_14,
  input  in_15,
  input  in_16,
  output out_17,
  output out_18,
  output out_19,
  output out_20,
  output out_21,
  output out_22,
  output out_23,
  output out_24,
  output out_25,
  output out_26,
  output out_27,
  output out_28,
  output out_29,
  output out_30,
  output out_31,
  output out_32
);

  xor xor_1 (out_32, in_1, in_1);

  assign out_17 = in_2;
  assign out_18 = in_3;
  assign out_19 = in_4;
  assign out_20 = in_5;
  assign out_21 = in_6;
  assign out_22 = in_7;
  assign out_23 = in_8;
  assign out_24 = in_9;
  assign out_25 = in_10;
  assign out_26 = in_11;
  assign out_27 = QUOCIENTE;
  assign out_28 = in_13;
  assign out_29 = in_14;
  assign out_30 = in_15;
  assign out_31 = in_16;

  // Notes on the sheet:
  //   RESTO (inicia zeado)
endmodule

module set_rightmost (
  input  q7,
  input  in_2,
  input  in_3,
  input  quociente,
  input  in_5,
  input  in_6,
  input  in_7,
  input  in_8,
  output out_9,
  output out_10,
  output out_11,
  output out_12,
  output out_13,
  output out_14,
  output out_15,
  output out_16
);

  xor xor_1 (out_16, in_8, 1'b1);

  assign out_9 = q7;
  assign out_10 = in_2;
  assign out_11 = in_3;
  assign out_12 = quociente;
  assign out_13 = in_5;
  assign out_14 = in_6;
  assign out_15 = in_7;
endmodule

module _8bitSub (
  input  c0,
  input  a0,
  input  a1,
  input  a2,
  input  a3,
  input  a4,
  input  a5,
  input  a6,
  input  a7,
  input  b0,
  input  b1,
  input  b2,
  input  b3,
  input  b4,
  input  b5,
  input  b6,
  input  b7,
  output out_18,
  output out_19,
  output out_20,
  output out_21,
  output out_22,
  output out_23,
  output out_24,
  output out_25,
  output sign
);

  wire not_1_out, subtract_1_ci_1, subtract_2_ci_1, subtract_3_ci_1, subtract_4_ci_1, subtract_5_ci_1,
       subtract_6_ci_1, subtract_7_ci_1;

  not not_1 (not_1_out, b0);
  subtract subtract_1 (.Ai(a0), .CI(c0), .SUM(out_18), .CI_1(subtract_1_ci_1), .Bi(not_1_out));
  subtract subtract_2 (.Ai(a1), .CI(subtract_1_ci_1), .SUM(out_19), .CI_1(subtract_2_ci_1), .Bi(b1));
  subtract subtract_3 (.Ai(a2), .CI(subtract_2_ci_1), .SUM(out_20), .CI_1(subtract_3_ci_1), .Bi(b2));
  subtract subtract_4 (.Ai(a3), .CI(subtract_3_ci_1), .SUM(out_21), .CI_1(subtract_4_ci_1), .Bi(b3));
  subtract subtract_5 (.Ai(a4), .CI(subtract_4_ci_1), .SUM(out_22), .CI_1(subtract_5_ci_1), .Bi(b4));
  subtract subtract_6 (.Ai(a5), .CI(subtract_5_ci_1), .SUM(out_23), .CI_1(subtract_6_ci_1), .Bi(b5));
  subtract subtract_7 (.Ai(a6), .CI(subtract_6_ci_1), .SUM(out_24), .CI_1(subtract_7_ci_1), .Bi(b6));
  subtract subtract_8 (.Ai(a7), .CI(subtract_7_ci_1), .SUM(out_25), .Bi(b7));  // open: CI_1

  assign sign = out_25;
endmodule
