// Logisim project subt8.circ as structural Verilog: 4 circuits, main circuit 8bitSub
module _8bitSub (
  input  c0,
  input  a0,
  input  a1,
  input  a2,
  input  a3,
  input  a4,
  input  a5,
  input  a6,
  input  a7,
  input  b0,
  input  b1,
  input  b2,
  input  b3,
  input  b4,
  input  b5,
  input  b6,
  input  b7,
  output out_18,
  output out_19,
  output out_20,
  output out_21,
  output out_22,
  output out_23,
  output out_24,
  output out_25
);

  wire not_1_out, subtract_1_ci_1, subtract_2_ci_1, subtract_3_ci_1, subtract_4_ci_1, subtract_5_ci_1,
       subtract_6_ci_1, subtract_7_ci_1;

  not not_1 (not_1_out, b0);
  subtract subtract_1 (.Ai(a0), .CI(c0), .SUM(out_18), .CI_1(subtract_1_ci_1), .Bi(not_1_out));
  subtract subtract_2 (.Ai(a1), .CI(subtract_1_ci_1), .SUM(out_19), .CI_1(subtract_2_ci_1), .Bi(b1));
  subtract subtract_3 (.Ai(a2), .CI(subtract_2_ci_1), .SUM(out_20), .CI_1(subtract_3_ci_1), .Bi(b2));
  subtract subtract_4 (.Ai(a3), .CI(subtract_3_ci_1), .SUM(out_21), .CI_1(subtract_4_ci_1), .Bi(b3));
  subtract subtract_5 (.Ai(a4), .CI(subtract_4_ci_1), .SUM(out_22), .CI_1(subtract_5_ci_1), .Bi(b4));
  subtract subtract_6 (.Ai(a5), .CI(subtract_5_ci_1), .SUM(out_23), .CI_1(subtract_6_ci_1), .Bi(b5));
  subtract subtract_7 (.Ai(a6), .CI(subtract_6_ci_1), .SUM(out_24), .CI_1(subtract_7_ci_1), .Bi(b6));
  subtract subtract_8 (.Ai(a7), .CI(subtract_7_ci_1), .SUM(out_25), .Bi(b7));  // open: CI_1
endmodule

module subtract (
  input  Ai,
  input  Bi,
  input  CI,
  output SUM,
  output CI_1
);

  wire and_1_out, and_2_out, not_1_out, xor_1_out;

  not not_1 (not_1_out, Bi);
  xor xor_1 (xor_1_out, Ai, not_1_out);
  and and_1 (and_1_out, Ai, not_1_out);
  and and_2 (and_2_out, xor_1_out, CI);
  or or_1 (CI_1, and_1_out, and_2_out);
  xor xor_2 (SUM, xor_1_out, CI);

  // Notes on the sheet:
  //   BI
endmodule

module main (
  input  [7:0] Remainder,
  input  [7:0] Quocient,
  input  [7:0] Divisor
);
endmodule

module Subcell (
  input  in_1,
  input  [7:0] A,
  input  [7:0] B,
  output [7:0] Sub
);

  _8bitSub u_8bitsub_1 (
    .out_18(Sub[0]), .out_19(Sub[1]), .out_20(Sub[2]), .out_21(Sub[3]), .out_22(Sub[4]), .out_23(Sub[5]),
    .out_24(Sub[6]), .out_25(Sub[7]), .a6(A[6]), .a7(A[7]), .c0(in_1), .a0(A[0]), .a1(A[1]), .a2(A[2]),
    .a3(A[3]), .a4(A[4]), .a5(A[5]), .b0(B[0]), .b1(B[1]), .b2(B[2]), .b3(B[3]), .b4(B[4]), .b5(B[5]),
    .b6(B[6]), .b7(B[7]));
endmodule
