// Logisim project CPU.circ as structural Verilog: 3 circuits, main circuit PC
module PC (
  input  clear,
  input  clock,
  input  set,
  input  [7:0] in_4,
  output [7:0] out_5
);

  wire and_1_out, and_2_out, and_3_out, and_4_out, and_5_out, and_6_out, and_7_out, controlled_buffer_1_out,
       controlled_buffer_4_out, controlled_buffer_6_out, controlled_buffer_7_out, controlled_buffer_9_out,
       controlled_buffer_11_out, controlled_buffer_13_out, controlled_buffer_15_out,
       controlled_buffer_17_out, not_1_out, not_2_out, not_3_out, not_4_out, not_5_out, not_6_out, not_7_out,
       not_8_out, not_9_out, not_10_out, not_11_out, not_12_out, not_13_out, not_14_out, not_15_out,
       not_16_out, not_17_out, not_18_out, not_19_out, not_20_out, not_21_out, not_22_out, not_23_out,
       not_24_out, not_25_out, pull_resistor_1_node, pull_resistor_2_node, pull_resistor_3_node,
       pull_resistor_4_node, pull_resistor_5_node, pull_resistor_6_node, pull_resistor_7_node,
       pull_resistor_8_node;

  and and_1 (and_1_out, out_5[0], out_5[1], out_5[2], out_5[3], out_5[4], out_5[5], out_5[6]);
  assign controlled_buffer_1_out = not_3_out ? controlled_buffer_17_out : 1'bz;  // Controlled_Buffer controlled_buffer_1
  not not_1 (not_1_out, not_2_out);
  not not_2 (not_2_out, pull_resistor_1_node);
  not not_3 (not_3_out, and_7_out);
  Pull_Resistor pull_resistor_1 (.node(pull_resistor_1_node));
  assign pull_resistor_1_node = and_7_out ? in_4[7] : 1'bz;  // Controlled_Buffer controlled_buffer_2
  and and_2 (and_2_out, out_5[0], out_5[1], out_5[2], out_5[3], out_5[4], out_5[5]);
  J_K_Flip_Flop j_k_ff_1 (
    .J(and_1_out), .clk(clock), .K(and_1_out), .Q(out_5[7]), .preset(not_1_out), .en(1'b1),
    .reset(controlled_buffer_1_out));  // open: Qn
  not not_4 (not_4_out, not_5_out);
  not not_5 (not_5_out, pull_resistor_2_node);
  assign controlled_buffer_1_out = and_7_out ? ~in_4[7] : 1'bz;  // Controlled_Inverter controlled_inverter_1
  Pull_Resistor pull_resistor_2 (.node(pull_resistor_2_node));
  assign pull_resistor_2_node = and_7_out ? in_4[6] : 1'bz;  // Controlled_Buffer controlled_buffer_3
  and and_3 (and_3_out, out_5[0], out_5[1], out_5[2], out_5[3], out_5[4]);
  J_K_Flip_Flop j_k_ff_2 (
    .J(and_2_out), .clk(clock), .K(and_2_out), .Q(out_5[6]), .preset(not_4_out), .en(1'b1),
    .reset(controlled_buffer_4_out));  // open: Qn
  assign controlled_buffer_4_out = not_8_out ? controlled_buffer_17_out : 1'bz;  // Controlled_Buffer controlled_buffer_4
  not not_6 (not_6_out, not_7_out);
  not not_7 (not_7_out, pull_resistor_3_node);
  not not_8 (not_8_out, and_7_out);
  assign controlled_buffer_4_out = and_7_out ? ~in_4[6] : 1'bz;  // Controlled_Inverter controlled_inverter_2
  Pull_Resistor pull_resistor_3 (.node(pull_resistor_3_node));
  assign pull_resistor_3_node = and_7_out ? in_4[5] : 1'bz;  // Controlled_Buffer controlled_buffer_5
  J_K_Flip_Flop j_k_ff_3 (
    .J(and_3_out), .clk(clock), .K(and_3_out), .Q(out_5[5]), .preset(not_6_out), .en(1'b1),
    .reset(controlled_buffer_6_out));  // open: Qn
  assign controlled_buffer_6_out = not_9_out ? controlled_buffer_17_out : 1'bz;  // Controlled_Buffer controlled_buffer_6
  not not_9 (not_9_out, and_7_out);
  assign controlled_buffer_6_out = and_7_out ? ~in_4[5] : 1'bz;  // Controlled_Inverter controlled_inverter_3
  and and_4 (and_4_out, out_5[0], out_5[1], out_5[2], out_5[3]);
  J_K_Flip_Flop j_k_ff_4 (
    .J(and_4_out), .clk(clock), .K(and_4_out), .Q(out_5[4]), .preset(not_10_out), .en(1'b1),
    .reset(controlled_buffer_7_out));  // open: Qn
  assign controlled_buffer_7_out = not_12_out ? controlled_buffer_17_out : 1'bz;  // Controlled_Buffer controlled_buffer_7
  not not_10 (not_10_out, not_11_out);
  not not_11 (not_11_out, pull_resistor_4_node);
  not not_12 (not_12_out, and_7_out);
  Pull_Resistor pull_resistor_4 (.node(pull_resistor_4_node));
  assign controlled_buffer_7_out = and_7_out ? ~in_4[4] : 1'bz;  // Controlled_Inverter controlled_inverter_4
  assign pull_resistor_4_node = and_7_out ? in_4[4] : 1'bz;  // Controlled_Buffer controlled_buffer_8
  and and_5 (and_5_out, out_5[0], out_5[1], out_5[2]);
  J_K_Flip_Flop j_k_ff_5 (
    .J(and_5_out), .clk(clock), .K(and_5_out), .Q(out_5[3]), .preset(not_13_out), .en(1'b1),
    .reset(controlled_buffer_9_out));  // open: Qn
  assign controlled_buffer_9_out = not_15_out ? controlled_buffer_17_out : 1'bz;  // Controlled_Buffer controlled_buffer_9
  not not_13 (not_13_out, not_14_out);
  not not_14 (not_14_out, pull_resistor_5_node);
  not not_15 (not_15_out, and_7_out);
  assign controlled_buffer_9_out = and_7_out ? ~in_4[3] : 1'bz;  // Controlled_Inverter controlled_inverter_5
  Pull_Resistor pull_resistor_5 (.node(pull_resistor_5_node));
  assign pull_resistor_5_node = and_7_out ? in_4[3] : 1'bz;  // Controlled_Buffer controlled_buffer_10
  J_K_Flip_Flop j_k_ff_6 (
    .J(and_6_out), .clk(clock), .K(and_6_out), .Q(out_5[2]), .preset(not_16_out), .en(1'b1),
    .reset(controlled_buffer_11_out));  // open: Qn
  assign controlled_buffer_11_out = not_18_out ? controlled_buffer_17_out : 1'bz;  // Controlled_Buffer controlled_buffer_11
  not not_16 (not_16_out, not_17_out);
  not not_17 (not_17_out, pull_resistor_6_node);
  not not_18 (not_18_out, and_7_out);
  Pull_Resistor pull_resistor_6 (.node(pull_resistor_6_node));
  assign controlled_buffer_11_out = and_7_out ? ~in_4[2] : 1'bz;  // Controlled_Inverter controlled_inverter_6
  assign pull_resistor_6_node = and_7_out ? in_4[2] : 1'bz;  // Controlled_Buffer controlled_buffer_12
  and and_6 (and_6_out, out_5[0], out_5[1]);
  J_K_Flip_Flop j_k_ff_7 (
    .J(out_5[0]), .clk(clock), .K(out_5[0]), .Q(out_5[1]), .preset(not_19_out), .en(1'b1),
    .reset(controlled_buffer_13_out));  // open: Qn
  assign controlled_buffer_13_out = not_21_out ? controlled_buffer_17_out : 1'bz;  // Controlled_Buffer controlled_buffer_13
  not not_19 (not_19_out, not_20_out);
  not not_20 (not_20_out, pull_resistor_7_node);
  not not_21 (not_21_out, and_7_out);
  Pull_Resistor pull_resistor_7 (.node(pull_resistor_7_node));
  assign controlled_buffer_13_out = and_7_out ? ~in_4[1] : 1'bz;  // Controlled_Inverter controlled_inverter_7
  assign pull_resistor_7_node = and_7_out ? in_4[1] : 1'bz;  // Controlled_Buffer controlled_buffer_14
  assign controlled_buffer_15_out = not_24_out ? controlled_buffer_17_out : 1'bz;  // Controlled_Buffer controlled_buffer_15
  not not_22 (not_22_out, not_23_out);
  not not_23 (not_23_out, pull_resistor_8_node);
  not not_24 (not_24_out, and_7_out);
  Pull_Resistor pull_resistor_8 (.node(pull_resistor_8_node));
  assign pull_resistor_8_node = and_7_out ? in_4[0] : 1'bz;  // Controlled_Buffer controlled_buffer_16
  J_K_Flip_Flop j_k_ff_8 (
    .J(1'b1), .clk(clock), .K(1'b1), .Q(out_5[0]), .preset(not_22_out), .en(1'b1),
    .reset(controlled_buffer_15_out));  // open: Qn
  assign controlled_buffer_17_out = not_24_out ? clear : 1'bz;  // Controlled_Buffer controlled_buffer_17
  assign controlled_buffer_15_out = and_7_out ? ~in_4[0] : 1'bz;  // Controlled_Inverter controlled_inverter_8
  not not_25 (not_25_out, clock);
  and and_7 (and_7_out, not_25_out, set);

  // Notes on the sheet:
  //   SET
endmodule

module Ctrl (
  input  [15:0] in_1,
  input  clock,
  output [7:0] out_3,
  output out_4,
  output out_5,
  output out_6,
  output out_7,
  output out_8,
  output out_9,
  output out_10
);

  wire JMP_out, LDA_out, not_1_out, STA_out, STP_out;
  wire [6:0] controlled_buffer_1_out;

  and LDA (LDA_out, in_1[8], in_1[9], ~in_1[10], in_1[11], ~in_1[12], ~in_1[13], ~in_1[14], ~in_1[15]);  // AND_Gate
  and STA (STA_out, ~in_1[8], ~in_1[9], in_1[10], in_1[11], ~in_1[12], ~in_1[13], ~in_1[14], ~in_1[15]);  // AND_Gate
  and JMP (JMP_out, in_1[8], in_1[9], ~in_1[10], ~in_1[11], in_1[12], in_1[13], ~in_1[14], ~in_1[15]);  // AND_Gate
  and STP (STP_out, ~in_1[8], in_1[9], in_1[10], ~in_1[11], ~in_1[12], ~in_1[13], in_1[14], ~in_1[15]);  // AND_Gate
  assign controlled_buffer_1_out = JMP_out ? 7'b0101010 : 7'bz;  // Controlled_Buffer controlled_buffer_1
  assign controlled_buffer_1_out = STP_out ? 7'b0101001 : 7'bz;  // Controlled_Buffer controlled_buffer_2
  not not_1 (not_1_out, clock);
  assign controlled_buffer_1_out = STA_out ? 7'b1000100 : 7'bz;  // Controlled_Buffer controlled_buffer_3
  assign out_4 = not_1_out ? controlled_buffer_1_out[6] : 1'bz;  // Controlled_Buffer controlled_buffer_4
  Pull_Resistor pull_resistor_1 (.node(out_4));
  assign controlled_buffer_1_out = LDA_out ? 7'b1110000 : 7'bz;  // Controlled_Buffer controlled_buffer_5
  assign out_5 = not_1_out ? controlled_buffer_1_out[5] : 1'bz;  // Controlled_Buffer controlled_buffer_6
  assign out_6 = not_1_out ? controlled_buffer_1_out[4] : 1'bz;  // Controlled_Buffer controlled_buffer_7
  Pull_Resistor pull_resistor_2 (.node(out_6));
  Pull_Resistor #(.pull(1)) pull_resistor_3 (.node(out_5));
  assign out_7 = not_1_out ? controlled_buffer_1_out[3] : 1'bz;  // Controlled_Buffer controlled_buffer_8
  Pull_Resistor #(.pull(1)) pull_resistor_4 (.node(out_7));
  assign out_8 = not_1_out ? controlled_buffer_1_out[2] : 1'bz;  // Controlled_Buffer controlled_buffer_9
  Pull_Resistor pull_resistor_5 (.node(out_8));
  assign out_9 = not_1_out ? controlled_buffer_1_out[1] : 1'bz;  // Controlled_Buffer controlled_buffer_10
  assign out_10 = not_1_out ? controlled_buffer_1_out[0] : 1'bz;  // Controlled_Buffer controlled_buffer_11
  Pull_Resistor pull_resistor_6 (.node(out_9));
  Pull_Resistor pull_resistor_7 (.node(out_10));

  assign out_3 = in_1[7:0];

  // Notes on the sheet:
  //   clock: pull=down
  //   Que significam:
  //   instrução
  //   São 7 bits que irão controlar, respectivamente:
  //   W_ctrl, RW, R_acc, R_ir, write_acc, set_pc, clear
  //   Essas constantes representam a execução da instrução.
  //   RW: Se a RAM estará em modo Read ou Write ( 1 para Read )
  //   endereço
  //   W_ctrl: Se quem vai dizer o proximo endereço para a RAM é o PC ou o Ctrl direto
  //   set_pc: informa o circuito do PC se ele deve ter seu valor mudado pelo controle ou não
  //   clear: informa o flip-flop que cuida do desligamento da CPU se ele deve desliga-lá ou não
  //   R_acc: controla o buffer que manda o conteudo da RAM para ACC ( ativado quando ACC deve receber um valor )
  //   R_ir: controla o buffer que manda o countedo da RAM para IR ( ativado quando IR deve receber uma instrução )
  //   01101010
  //   01101001
  //   write_acc: controla o buffer que manda o conteúdo de ACC para RAM ( ativado se o conteúdo de ACC deve ser escrito na RAM )
  //   11000000
  //   10000100
  //   Execução
  //   default:NOP
endmodule

module CPU (
  output [15:0] out_1,
  output [15:0] out_2,
  output [15:0] out_3,
  output [7:0] out_4
);

  wire and_1_out, \begin , button_1_out, clear, clock_1_out, clock_2_out, clock_3_out, clock_4_out,
       clock_5_out, clock_6_out, ctrl_1_out_4, ctrl_1_out_5, ctrl_1_out_6, ctrl_1_out_7, ctrl_1_out_8,
       ctrl_1_out_9, ctrl_1_out_10, j_k_ff_2_qn, ligado, not_1_out, not_2_out, not_3_out, not_4_out,
       not_5_out;
  wire [7:0] ctrl_1_out_3, pc_1_out_5;
  wire [15:0] controlled_buffer_3_out, controlled_buffer_4_out, register_1_q;

  assign out_4 = not_1_out ? pc_1_out_5 : 8'bz;  // Controlled_Buffer controlled_buffer_1
  not not_1 (not_1_out, ctrl_1_out_4);
  PC pc_1 (.clear(clear), .clock(and_1_out), .set(ctrl_1_out_9), .out_5(pc_1_out_5), .in_4(ctrl_1_out_3));
  not not_2 (not_2_out, clock_1_out);
  Clock clock_1 (.out(clock_1_out));
  and and_1 (and_1_out, not_2_out, \begin );
  assign out_4 = ctrl_1_out_4 ? ctrl_1_out_3 : 8'bz;  // Controlled_Buffer controlled_buffer_2
  not not_3 (not_3_out, clock_2_out);
  Clock clock_2 (.out(clock_2_out));
  RAM #(.dataWidth(16)) ram_1 (
    .addr(out_4), .data(out_1), .sel(ligado), .clk(not_4_out), .ld(ctrl_1_out_5));  // open: clr
  not not_4 (not_4_out, clock_3_out);
  Clock clock_3 (.out(clock_3_out));
  assign controlled_buffer_3_out = ctrl_1_out_6 ? out_1 : 16'bz;  // Controlled_Buffer controlled_buffer_3
  Clock clock_4 (.out(clock_4_out));
  assign controlled_buffer_4_out = ctrl_1_out_7 ? out_1 : 16'bz;  // Controlled_Buffer controlled_buffer_4
  assign out_1 = ctrl_1_out_8 ? register_1_q : 16'bz;  // Controlled_Buffer controlled_buffer_5
  Register #(.width(16), .trigger("high")) register_1 (
    .D(controlled_buffer_3_out), .en(ligado), .Q(register_1_q), .clk(clock_4_out), .clr(clear));
  Ctrl ctrl_1 (
    .in_1(out_2), .clock(not_3_out), .out_3(ctrl_1_out_3), .out_4(ctrl_1_out_4), .out_5(ctrl_1_out_5),
    .out_6(ctrl_1_out_6), .out_7(ctrl_1_out_7), .out_8(ctrl_1_out_8), .out_9(ctrl_1_out_9),
    .out_10(ctrl_1_out_10));
  Register #(.width(16), .trigger("high")) register_2 (
    .D(controlled_buffer_4_out), .en(ligado), .Q(out_2), .clk(not_5_out), .clr(clear));
  not not_5 (not_5_out, clock_5_out);
  Clock clock_5 (.out(clock_5_out));
  Clock clock_6 (.out(clock_6_out));
  Button button_1 (.out(button_1_out));
  J_K_Flip_Flop j_k_ff_1 (
    .J(1'b1), .clk(clock_6_out), .K(1'b0), .Q(\begin ), .en(ligado), .reset(clear));  // open: Qn, preset
  J_K_Flip_Flop j_k_ff_2 (
    .J(1'b1), .clk(button_1_out), .K(1'b1), .Q(ligado), .Qn(j_k_ff_2_qn), .en(1'b1), .reset(ctrl_1_out_10));  // open: preset
  or or_1 (clear, j_k_ff_2_qn, ctrl_1_out_10);

  assign out_3 = out_1;

  // Other names for the same wires on the sheet: A[7:0] = out_4; ACC[15:0] = out_1; D[15:0] = out_1; IR[15:0] = out_2

  // Notes on the sheet:
  //   Para ligar a CPU, pressionar o botao START
  //   R_ir
  //   ACC
  //   IR
  //   START
  //   Valores:
  //   a instrucao STP desliga a CPU
  //   Como o PC se auto-incrementa quando recebe o clock,
  //   esse flip-flop impede que ele faça isso no primeiro pulso.
endmodule
